// Logisim project CPU_1.circ as structural Verilog: 12 circuits, main circuit main
module main (
  input  Reset,
  output [31:0] out_2,
  output out_3,
  output [4:0] out_4,
  output [31:0] out_5,
  output out_6,
  output [4:0] out_7,
  output [31:0] out_8
);

  wire B, Clk, controller_1_alusrc, controller_1_extop, controller_1_memtoreg, controller_1_regdst,
       controller_1_sllen, J, multiplexer_1_out;
  wire [3:0] controller_1_aluctr;
  wire [31:0] dm_1_d, ext_1_out_3, grf_1_rd1, MemAddr, multiplexer_3_out, multiplexer_4_out, shifter_1_out,
       sll;

  Clock u_Clk (.out(Clk));
  Multiplexer multiplexer_1 (.in0(1'b0), .in1(MemAddr[0]), .out(multiplexer_1_out), .sel(B));  // open: en
  IFU ifu_1 (.Clk(Clk), .Reset(Reset), .Branch(multiplexer_1_out), .Instr(out_2), .J(J));
  Controller controller_1 (
    .OpCode(out_2[31:26]), .Func(out_2[5:0]), .RegDst(controller_1_regdst), .ALUSrc(controller_1_alusrc),
    .MemtoReg(controller_1_memtoreg), .RegWrite(out_3), .MemWrite(out_6), .Branch(B),
    .ExtOp(controller_1_extop), .ALUctr(controller_1_aluctr), .JEn(J), .SllEn(controller_1_sllen));
  assign sll = {{27{1'b0}}, out_2[10:6]};  // Bit_Extender bit_extender_1
  Multiplexer #(.width(5)) multiplexer_2 (
    .in0(out_2[20:16]), .in1(out_2[15:11]), .out(out_4), .sel(controller_1_regdst));  // open: en
  EXT ext_1 (.Imm16(out_2[15:0]), .ExtOp(controller_1_extop), .out_3(ext_1_out_3));
  GRF grf_1 (
    .WD(out_5), .Reset(Reset), .Clk(Clk), .WE(out_3), .A3(out_4), .A1(out_2[25:21]), .A2(out_2[20:16]),
    .RD1(grf_1_rd1), .RD2(out_8));
  Multiplexer #(.width(32)) multiplexer_3 (
    .in0(grf_1_rd1), .in1(sll), .out(multiplexer_3_out), .sel(controller_1_sllen));  // open: en
  Multiplexer #(.width(32)) multiplexer_4 (
    .in0(out_8), .in1(ext_1_out_3), .out(multiplexer_4_out), .sel(controller_1_alusrc));  // open: en
  ALU alu_1 (.SrcA(multiplexer_3_out), .SrcB(multiplexer_4_out), .ALUOp(controller_1_aluctr), .ALUResult(MemAddr));
  DM dm_1 (.A(MemAddr), .WD(out_8), .WE(out_6), .D(dm_1_d), .Clk(Clk), .in_4(Reset));
  Multiplexer #(.width(32)) multiplexer_5 (
    .in0(MemAddr), .in1(dm_1_d), .out(out_5), .sel(controller_1_memtoreg));  // open: en
  Shifter #(.width(32), .shift("lr")) shifter_1 (.in(MemAddr), .\dist (5'b00010), .out(shifter_1_out));
  Bit_Extender #(.in_width(32), .out_width(5)) bit_extender_2 (.in(shifter_1_out), .out(out_7));

  // Other names for the same wires on the sheet: Instr[31:0] = out_2; MemData[31:0] = out_8; MemWrite = out_6;
  //   RegAddr[4:0] = out_4; RegData[31:0] = out_5; RegWrite = out_3; Rst = Reset
endmodule

module IFU (
  input  Clk,
  input  Reset,
  input  Branch,
  input  J,
  output [31:0] Instr
);

  wire [31:0] bit_extender_1_out, npc_1_npc, PC_q;

  assign bit_extender_1_out = {{16{Instr[15]}}, Instr[15:0]};  // Bit_Extender bit_extender_1
  NPC npc_1 (.branch(Branch), .BOffset(bit_extender_1_out), .pc(PC_q), .npc(npc_1_npc), .J(J), .index(Instr[25:0]));
  Register #(.width(32)) PC (.D(npc_1_npc), .Q(PC_q), .clk(Clk), .clr(Reset));  // open: en
  IM im_1 (.PC(PC_q), .Instr(Instr));

  // Other names for the same wires on the sheet: c = Clk; r = Reset
endmodule

module NPC (
  input  branch,
  input  [31:0] BOffset,
  input  [31:0] pc,
  input  [25:0] index,
  input  J,
  output [31:0] npc
);

  wire [27:0] bit_extender_1_out, shifter_2_out;
  wire [31:0] adder_1_out, adder_2_out, multiplexer_1_out, shifter_1_out, subtractor_1_out;

  assign bit_extender_1_out = {{2{1'b0}}, index};  // Bit_Extender bit_extender_1
  Shifter #(.width(32)) shifter_1 (.in(BOffset), .\dist (5'b00010), .out(shifter_1_out));
  Adder #(.width(32)) adder_1 (.a(pc), .b(32'h4), .out(adder_1_out));  // open: cin, cout
  Shifter #(.width(28)) shifter_2 (.in(bit_extender_1_out), .\dist (5'b00010), .out(shifter_2_out));
  Multiplexer #(.width(32)) multiplexer_1 (
    .in0({32{1'b0}}), .in1(shifter_1_out), .out(multiplexer_1_out), .sel(branch));  // open: en
  // Probe on multiplexer_1_out
  Adder #(.width(32)) adder_2 (.a(multiplexer_1_out), .b(adder_1_out), .out(adder_2_out));  // open: cin, cout
  Subtractor #(.width(32)) subtractor_1 (
    .a({pc[31:28], shifter_2_out}), .b(32'h3000), .out(subtractor_1_out));  // open: bin, bout
  Multiplexer #(.width(32)) multiplexer_2 (.in0(adder_2_out), .in1(subtractor_1_out), .out(npc), .sel(J));  // open: en
endmodule

module IM (
  input  [31:0] PC,
  output [31:0] Instr
);

  wire comparator_1_eq, comparator_1_lt, or_1_out;
  wire [9:0] bit_extender_1_out;
  wire [31:0] rom_1_data, shifter_1_out;

  Shifter #(.width(32), .shift("ar")) shifter_1 (.in(PC), .\dist (5'b00010), .out(shifter_1_out));
  Bit_Extender #(.in_width(32), .out_width(10)) bit_extender_1 (.in(shifter_1_out), .out(bit_extender_1_out));
  Comparator #(.width(32), .mode("unsigned")) comparator_1 (
    .a(shifter_1_out), .b(32'h3fe), .eq(comparator_1_eq), .lt(comparator_1_lt));  // open: gt
  ROM #(.addrWidth(10), .dataWidth(32)) rom_1 (.addr(bit_extender_1_out), .data(rom_1_data));  // open: sel
  or or_1 (or_1_out, comparator_1_eq, comparator_1_lt);
  Multiplexer #(.width(32)) multiplexer_1 (
    .in0({32{1'b0}}), .in1(rom_1_data), .out(Instr), .sel(or_1_out));  // open: en
endmodule

module Controller (
  input  [5:0] OpCode,
  input  [5:0] Func,
  output RegDst,
  output ALUSrc,
  output MemtoReg,
  output RegWrite,
  output MemWrite,
  output Branch,
  output JEn,
  output SllEn,
  output ExtOp,
  output [3:0] ALUctr
);

  wire comparator_1_eq, \i或j译码_1_addi , \i或j译码_1_beq , \i或j译码_1_j , \i或j译码_1_lui , \i或j译码_1_lw ,
       \i或j译码_1_ori , \i或j译码_1_sw , not_1_out, \r型译码_1_add , \r型译码_1_sll , \r型译码_1_sllv , \r型译码_1_slt ,
       \r型译码_1_sub ;

  Comparator #(.width(6), .mode("unsigned")) comparator_1 (
    .a(OpCode), .b({6{1'b0}}), .eq(comparator_1_eq));  // open: gt, lt
  not not_1 (not_1_out, comparator_1_eq);
  \R型译码  \r型译码_1  (
    .Func(Func), .En(comparator_1_eq), .add(\r型译码_1_add ), .sub(\r型译码_1_sub ), .sll(\r型译码_1_sll ),
    .sllv(\r型译码_1_sllv ), .slt(\r型译码_1_slt ));
  \I或J译码  \i或j译码_1  (
    .OpCode(OpCode), .En(not_1_out), .beq(\i或j译码_1_beq ), .ori(\i或j译码_1_ori ), .lui(\i或j译码_1_lui ),
    .lw(\i或j译码_1_lw ), .sw(\i或j译码_1_sw ), .addi(\i或j译码_1_addi ), .j(\i或j译码_1_j ));
  \或逻辑  \u_或逻辑_1  (
    .add(\r型译码_1_add ), .sub(\r型译码_1_sub ), .beq(\i或j译码_1_beq ), .ori(\i或j译码_1_ori ), .lui(\i或j译码_1_lui ),
    .lw(\i或j译码_1_lw ), .sw(\i或j译码_1_sw ), .RegDst(RegDst), .ALUSrc(ALUSrc), .MemtoReg(MemtoReg),
    .RegWrite(RegWrite), .MemWrite(MemWrite), .Branch(Branch), .ExtOp(ExtOp), .ALUctr_2(ALUctr[2]),
    .ALUctr_1(ALUctr[1]), .ALUctr_0(ALUctr[0]), .ALUctr_3(ALUctr[3]), .sll(\r型译码_1_sll ),
    .sllv(\r型译码_1_sllv ), .slt(\r型译码_1_slt ), .addi(\i或j译码_1_addi ), .j(\i或j译码_1_j ), .JEn(JEn), .SllEn(SllEn));
endmodule

module \R型译码  (
  input  [5:0] Func,
  input  En,
  output add,
  output sub,
  output sll,
  output sllv,
  output slt
);

  wire decoder_1_out0, decoder_1_out1;

  Decoder #(.disabled(0)) decoder_1 (.out0(decoder_1_out0), .out1(decoder_1_out1), .sel(Func[5]), .en(En));
  Decoder #(.select(5), .disabled(0)) decoder_2 (
    .out0(sll), .out4(sllv), .sel(Func[4:0]), .en(decoder_1_out0));  // open: out1, out2, out3, out5, out6, out7, out8, out9, out10, out11, out12, out13, out14, out15, out16, out17, out18, out19, out20, out21, out22, out23, out24, out25, out26, out27, out28, out29, out30, out31
  Decoder #(.select(5), .disabled(0)) decoder_3 (
    .out0(add), .out2(sub), .out10(slt), .sel(Func[4:0]), .en(decoder_1_out1));  // open: out1, out3, out4, out5, out6, out7, out8, out9, out11, out12, out13, out14, out15, out16, out17, out18, out19, out20, out21, out22, out23, out24, out25, out26, out27, out28, out29, out30, out31
endmodule

module \I或J译码  (
  input  [5:0] OpCode,
  input  En,
  output beq,
  output ori,
  output lui,
  output lw,
  output sw,
  output addi,
  output j
);

  wire decoder_1_out0, decoder_1_out1;

  Decoder #(.disabled(0)) decoder_1 (.out0(decoder_1_out0), .out1(decoder_1_out1), .sel(OpCode[5]), .en(En));
  Decoder #(.select(5), .disabled(0)) decoder_2 (
    .out2(j), .out4(beq), .out8(addi), .out13(ori), .out15(lui), .sel(OpCode[4:0]), .en(decoder_1_out0));  // open: out0, out1, out3, out5, out6, out7, out9, out10, out11, out12, out14, out16, out17, out18, out19, out20, out21, out22, out23, out24, out25, out26, out27, out28, out29, out30, out31
  Decoder #(.select(5), .disabled(0)) decoder_3 (
    .out3(lw), .out11(sw), .sel(OpCode[4:0]), .en(decoder_1_out1));  // open: out0, out1, out2, out4, out5, out6, out7, out8, out9, out10, out12, out13, out14, out15, out16, out17, out18, out19, out20, out21, out22, out23, out24, out25, out26, out27, out28, out29, out30, out31
endmodule

module \或逻辑  (
  input  add,
  input  sub,
  input  sll,
  input  sllv,
  input  slt,
  input  beq,
  input  ori,
  input  lui,
  input  lw,
  input  sw,
  input  addi,
  input  j,
  output RegDst,
  output ALUSrc,
  output MemtoReg,
  output RegWrite,
  output MemWrite,
  output Branch,
  output JEn,
  output SllEn,
  output ExtOp,
  output ALUctr_3,
  output ALUctr_2,
  output ALUctr_1,
  output ALUctr_0
);

  or or_1 (RegDst, add, sub, sll, sllv, slt);
  or or_2 (ALUSrc, ori, lui, lw, sw, addi);
  buf or_3 (MemtoReg, lw);  // OR_Gate
  or or_4 (RegWrite, addi, sllv, add, sub, ori, lui, lw, sll, slt);
  buf or_5 (MemWrite, sw);  // OR_Gate
  buf or_6 (Branch, beq);  // OR_Gate
  buf or_7 (JEn, j);  // OR_Gate
  buf or_8 (SllEn, sll);  // OR_Gate
  or or_9 (ExtOp, lw, sw, addi);
  or or_10 (ALUctr_3, sll, sllv, slt);
  or or_11 (ALUctr_2, sub, beq, lui);
  or or_12 (ALUctr_1, sllv, sll, add, sub, beq, lw, sw, addi);
  or or_13 (ALUctr_0, sllv, beq, ori, lui, slt, sll);
endmodule

module GRF (
  input  [31:0] WD,
  input  Clk,
  input  Reset,
  input  WE,
  input  [4:0] A3,
  input  [4:0] A1,
  input  [4:0] A2,
  output [31:0] RD1,
  output [31:0] RD2
);

  wire [31:0] _0, _1, _2, _3, _4, _5, _6, _7, _8, _9, _10, _11, _12, _13, _14, _15, _16, _17, _18, _19, _20,
       _21, _22, _23, _24, _25, _26, _27, _28, _29, _30, _31, demultiplexer_1_out0, demultiplexer_1_out1,
       demultiplexer_1_out2, demultiplexer_1_out3, demultiplexer_1_out4, demultiplexer_1_out5,
       demultiplexer_1_out6, demultiplexer_1_out7, demultiplexer_1_out8, demultiplexer_1_out9,
       demultiplexer_1_out10, demultiplexer_1_out11, demultiplexer_1_out12, demultiplexer_1_out13,
       demultiplexer_1_out14, demultiplexer_1_out15, demultiplexer_1_out16, demultiplexer_1_out17,
       demultiplexer_1_out18, demultiplexer_1_out19, demultiplexer_1_out20, demultiplexer_1_out21,
       demultiplexer_1_out22, demultiplexer_1_out23, demultiplexer_1_out24, demultiplexer_1_out25,
       demultiplexer_1_out26, demultiplexer_1_out27, demultiplexer_1_out28, demultiplexer_1_out29,
       demultiplexer_1_out30, demultiplexer_1_out31;

  Demultiplexer #(.select(5), .width(32), .tristate("true")) demultiplexer_1 (
    .out0(demultiplexer_1_out0), .out1(demultiplexer_1_out1), .out2(demultiplexer_1_out2),
    .out3(demultiplexer_1_out3), .out4(demultiplexer_1_out4), .out5(demultiplexer_1_out5),
    .out6(demultiplexer_1_out6), .out7(demultiplexer_1_out7), .out8(demultiplexer_1_out8),
    .out9(demultiplexer_1_out9), .out10(demultiplexer_1_out10), .out11(demultiplexer_1_out11),
    .out12(demultiplexer_1_out12), .out13(demultiplexer_1_out13), .out14(demultiplexer_1_out14),
    .out15(demultiplexer_1_out15), .out16(demultiplexer_1_out16), .out17(demultiplexer_1_out17),
    .out18(demultiplexer_1_out18), .out19(demultiplexer_1_out19), .out20(demultiplexer_1_out20),
    .out21(demultiplexer_1_out21), .out22(demultiplexer_1_out22), .out23(demultiplexer_1_out23),
    .out24(demultiplexer_1_out24), .out25(demultiplexer_1_out25), .out26(demultiplexer_1_out26),
    .out27(demultiplexer_1_out27), .out28(demultiplexer_1_out28), .out29(demultiplexer_1_out29),
    .out30(demultiplexer_1_out30), .out31(demultiplexer_1_out31), .in(WD), .sel(A3));  // open: en
  Register #(.width(32)) register_1 (.D(demultiplexer_1_out0), .Q(_0), .clk(Clk), .clr(1'b1));  // open: en
  Register #(.width(32)) register_2 (.D(demultiplexer_1_out4), .en(WE), .Q(_4), .clk(Clk), .clr(Reset));
  Register #(.width(32)) register_3 (.D(demultiplexer_1_out8), .en(WE), .Q(_8), .clk(Clk), .clr(Reset));
  Register #(.width(32)) register_4 (.D(demultiplexer_1_out12), .en(WE), .Q(_12), .clk(Clk), .clr(Reset));
  Register #(.width(32)) register_5 (.D(demultiplexer_1_out16), .en(WE), .Q(_16), .clk(Clk), .clr(Reset));
  Register #(.width(32)) register_6 (.D(demultiplexer_1_out20), .en(WE), .Q(_20), .clk(Clk), .clr(Reset));
  Register #(.width(32)) register_7 (.D(demultiplexer_1_out24), .en(WE), .Q(_24), .clk(Clk), .clr(Reset));
  Register #(.width(32)) register_8 (.D(demultiplexer_1_out28), .en(WE), .Q(_28), .clk(Clk), .clr(Reset));
  Register #(.width(32)) register_9 (.D(demultiplexer_1_out1), .en(WE), .Q(_1), .clk(Clk), .clr(Reset));
  Register #(.width(32)) register_10 (.D(demultiplexer_1_out5), .en(WE), .Q(_5), .clk(Clk), .clr(Reset));
  Register #(.width(32)) register_11 (.D(demultiplexer_1_out9), .en(WE), .Q(_9), .clk(Clk), .clr(Reset));
  Register #(.width(32)) register_12 (.D(demultiplexer_1_out13), .en(WE), .Q(_13), .clk(Clk), .clr(Reset));
  Register #(.width(32)) register_13 (.D(demultiplexer_1_out17), .en(WE), .Q(_17), .clk(Clk), .clr(Reset));
  Register #(.width(32)) register_14 (.D(demultiplexer_1_out21), .en(WE), .Q(_21), .clk(Clk), .clr(Reset));
  Register #(.width(32)) register_15 (.D(demultiplexer_1_out25), .en(WE), .Q(_25), .clk(Clk), .clr(Reset));
  Register #(.width(32)) register_16 (.D(demultiplexer_1_out29), .en(WE), .Q(_29), .clk(Clk), .clr(Reset));
  Register #(.width(32)) register_17 (.D(demultiplexer_1_out2), .en(WE), .Q(_2), .clk(Clk), .clr(Reset));
  Register #(.width(32)) register_18 (.D(demultiplexer_1_out6), .en(WE), .Q(_6), .clk(Clk), .clr(Reset));
  Register #(.width(32)) register_19 (.D(demultiplexer_1_out10), .en(WE), .Q(_10), .clk(Clk), .clr(Reset));
  Register #(.width(32)) register_20 (.D(demultiplexer_1_out14), .en(WE), .Q(_14), .clk(Clk), .clr(Reset));
  Register #(.width(32)) register_21 (.D(demultiplexer_1_out18), .en(WE), .Q(_18), .clk(Clk), .clr(Reset));
  Register #(.width(32)) register_22 (.D(demultiplexer_1_out22), .en(WE), .Q(_22), .clk(Clk), .clr(Reset));
  Register #(.width(32)) register_23 (.D(demultiplexer_1_out26), .en(WE), .Q(_26), .clk(Clk), .clr(Reset));
  Register #(.width(32)) register_24 (.D(demultiplexer_1_out30), .en(WE), .Q(_30), .clk(Clk), .clr(Reset));
  Register #(.width(32)) register_25 (.D(demultiplexer_1_out3), .en(WE), .Q(_3), .clk(Clk), .clr(Reset));
  Register #(.width(32)) register_26 (.D(demultiplexer_1_out7), .en(WE), .Q(_7), .clk(Clk), .clr(Reset));
  Register #(.width(32)) register_27 (.D(demultiplexer_1_out11), .en(WE), .Q(_11), .clk(Clk), .clr(Reset));
  Register #(.width(32)) register_28 (.D(demultiplexer_1_out15), .en(WE), .Q(_15), .clk(Clk), .clr(Reset));
  Register #(.width(32)) register_29 (.D(demultiplexer_1_out19), .en(WE), .Q(_19), .clk(Clk), .clr(Reset));
  Register #(.width(32)) register_30 (.D(demultiplexer_1_out23), .en(WE), .Q(_23), .clk(Clk), .clr(Reset));
  Register #(.width(32)) register_31 (.D(demultiplexer_1_out27), .en(WE), .Q(_27), .clk(Clk), .clr(Reset));
  Register #(.width(32)) register_32 (.D(demultiplexer_1_out31), .en(WE), .Q(_31), .clk(Clk), .clr(Reset));
  Multiplexer #(.select(5), .width(32)) multiplexer_1 (
    .in0(_0), .in1(_1), .in2(_2), .in3(_3), .in4(_4), .in5(_5), .in6(_6), .in7(_7), .in8(_8), .in9(_9),
    .in10(_10), .in11(_11), .in12(_12), .in13(_13), .in14(_14), .in15(_15), .in16(_16), .in17(_17),
    .in18(_18), .in19(_19), .in20(_20), .in21(_21), .in22(_22), .in23(_23), .in24(_24), .in25(_25),
    .in26(_26), .in27(_27), .in28(_28), .in29(_29), .in30(_30), .in31(_31), .out(RD1), .sel(A1));  // open: en
  Multiplexer #(.select(5), .width(32)) multiplexer_2 (
    .in0(_0), .in1(_1), .in2(_2), .in3(_3), .in4(_4), .in5(_5), .in6(_6), .in7(_7), .in8(_8), .in9(_9),
    .in10(_10), .in11(_11), .in12(_12), .in13(_13), .in14(_14), .in15(_15), .in16(_16), .in17(_17),
    .in18(_18), .in19(_19), .in20(_20), .in21(_21), .in22(_22), .in23(_23), .in24(_24), .in25(_25),
    .in26(_26), .in27(_27), .in28(_28), .in29(_29), .in30(_30), .in31(_31), .out(RD2), .sel(A2));  // open: en

  // Other names for the same wires on the sheet: en = WE; rst = Reset
endmodule

module ALU (
  input  [31:0] SrcA,
  input  [31:0] SrcB,
  input  [3:0] ALUOp,
  output [31:0] ALUResult
);

  wire comparator_1_eq, comparator_2_lt, comparator_3_gt;
  wire [4:0] bit_extender_1_out, bit_extender_2_out;
  wire [31:0] _0000, _0001, _0010, _0011, _0100, _0101, _0110, _0111, _1000, _1001, _1010, _1011, not_1_out,
       not_2_out, shifter_1_out, shifter_2_out, shifter_3_out;

  assign _0000 = SrcA & SrcB;  // AND_Gate and_1, 32 bits wide
  assign _0001 = SrcA | SrcB;  // OR_Gate or_1, 32 bits wide
  Adder #(.width(32)) adder_1 (.a(SrcA), .b(SrcB), .out(_0010));  // open: cin, cout
  assign not_1_out = ~SrcA;  // NOT_Gate not_1, 32 bits wide
  assign _0011 = not_1_out & SrcB;  // AND_Gate and_2, 32 bits wide
  assign _0100 = SrcA & not_2_out;  // AND_Gate and_3, 32 bits wide
  assign not_2_out = ~SrcB;  // NOT_Gate not_2, 32 bits wide
  Shifter #(.width(32)) shifter_1 (.in(SrcA), .\dist (5'b10000), .out(shifter_1_out));
  Shifter #(.width(32)) shifter_2 (.in(SrcB), .\dist (5'b10000), .out(shifter_2_out));
  Subtractor #(.width(32)) subtractor_1 (.a(SrcA), .b(SrcB), .out(_0110));  // open: bin, bout
  Comparator #(.width(32)) comparator_1 (.a(SrcA), .b(SrcB), .eq(comparator_1_eq));  // open: gt, lt
  Bit_Extender #(.in_width(32), .out_width(5)) bit_extender_1 (.in(SrcB), .out(bit_extender_1_out));
  Comparator #(.width(32)) comparator_2 (.a(SrcA), .b(SrcB), .lt(comparator_2_lt));  // open: gt, eq
  Comparator #(.width(32)) comparator_3 (.a(SrcA), .b(SrcB), .gt(comparator_3_gt));  // open: eq, lt
  Bit_Extender #(.in_width(32), .out_width(5)) bit_extender_2 (.in(SrcA), .out(bit_extender_2_out));
  Shifter #(.width(32), .shift("lr")) shifter_3 (.in(shifter_1_out), .\dist (5'b10000), .out(shifter_3_out));
  Shifter #(.width(32)) shifter_4 (.in(SrcA), .\dist (bit_extender_1_out), .out(_1000));
  Shifter #(.width(32)) shifter_5 (.in(SrcB), .\dist (bit_extender_2_out), .out(_1011));
  assign _0101 = shifter_3_out | shifter_2_out;  // OR_Gate or_2, 32 bits wide
  assign _0111 = {{31{1'b0}}, comparator_1_eq};  // Bit_Extender bit_extender_3
  assign _1001 = {{31{1'b0}}, comparator_2_lt};  // Bit_Extender bit_extender_4
  assign _1010 = {{31{1'b0}}, comparator_3_gt};  // Bit_Extender bit_extender_5
  Multiplexer #(.select(4), .width(32)) multiplexer_1 (
    .in0(_0000), .in1(_0001), .in2(_0010), .in3(_0011), .in4(_0100), .in5(_0101), .in6(_0110), .in7(_0111),
    .in8(_1000), .in9(_1001), .in10(_1010), .in11(_1011), .out(ALUResult), .sel(ALUOp));  // open: in12, in13, in14, in15, en

  // Other names for the same wires on the sheet: A[31:0] = SrcA; B[31:0] = SrcB
endmodule

module DM (
  input  [31:0] A,
  input  [31:0] WD,
  input  Clk,
  input  in_4,
  input  WE,
  output [31:0] D
);

  wire [9:0] bit_extender_1_out;
  wire [31:0] shifter_1_out;

  Shifter #(.width(32), .shift("lr")) shifter_1 (.in(A), .\dist (5'b00010), .out(shifter_1_out));
  Bit_Extender #(.in_width(32), .out_width(10)) bit_extender_1 (.in(shifter_1_out), .out(bit_extender_1_out));
  RAM #(.addrWidth(10), .dataWidth(32), .bus("separate")) ram_1 (
    .addr(bit_extender_1_out), .din(WD), .data(D), .str(WE), .clk(Clk), .clr(in_4));  // open: sel, ld
endmodule

module EXT (
  input  [15:0] Imm16,
  input  ExtOp,
  output [31:0] out_3
);

  wire [31:0] bit_extender_1_out, bit_extender_2_out;

  assign bit_extender_1_out = {{16{1'b0}}, Imm16};  // Bit_Extender bit_extender_1
  assign bit_extender_2_out = {{16{Imm16[15]}}, Imm16};  // Bit_Extender bit_extender_2
  Multiplexer #(.width(32)) multiplexer_1 (
    .in0(bit_extender_1_out), .in1(bit_extender_2_out), .out(out_3), .sel(ExtOp));  // open: en
endmodule
