// Logisim project CPU_0.circ as structural Verilog: 16 circuits, main circuit main
module main (
  input  Reset
);

  wire B, Clk, controller_1_alusrc, controller_1_byte, controller_1_jal, controller_1_memtoreg,
       controller_1_memwrite, controller_1_regwrite, cu_e_1_out_12, cu_e_1_out_13, cu_e_1_out_14,
       cu_e_1_out_15, cu_e_1_out_18, cu_e_1_out_19, cu_m_1_out_9, cu_m_1_out_10, cu_m_1_out_11,
       cu_m_1_out_12, cu_m_1_out_13, cu_w_1_out_7, cu_w_1_out_9, EO, JEn, Jr, multiplexer_1_out, RD, RW;
  wire [0:0] undriven;
  wire [1:0] controller_1_tnew, cu_e_1_out_20, cu_m_1_out_14, Tnew_W;
  wire [3:0] controller_1_aluctr, cu_e_1_out_17;
  wire [4:0] A3_W, multiplexer_2_out, multiplexer_3_out, register_6_q, register_12_q;
  wire [31:0] A, alu_1_aluresult, \dm新_1_d , ext_1_out_3, grf_1_rd2, ifu_1_instr, ifu_1_npc, ifu_1_out_10,
       multiplexer_4_out, multiplexer_5_out, register_1_q, register_2_q, register_3_q, register_4_q,
       register_5_q, register_7_q, register_8_q, register_9_q, register_10_q, register_11_q, register_13_q,
       register_14_q, register_16_q, register_18_q, register_19_q, WD, \输入到GRF ;

  Clock u_Clk (.out(Clk));
  Multiplexer multiplexer_1 (.in0(1'b0), .in1(undriven[0]), .out(multiplexer_1_out), .sel(B));  // open: en
  IFU ifu_1 (
    .Clk(Clk), .Reset(Reset), .Branch(multiplexer_1_out), .Instr(ifu_1_instr), .J(JEn), .NPC(ifu_1_npc),
    .jr(Jr), .A(A), .BO(ext_1_out_3), .out_10(ifu_1_out_10));
  Register #(.width(32)) register_1 (.D(ifu_1_out_10), .Q(register_1_q), .clk(Clk), .clr(Reset));  // open: en
  Register #(.width(32)) register_2 (.D(ifu_1_npc), .Q(register_2_q), .clk(Clk), .clr(Reset));  // open: en
  Register #(.width(32)) register_3 (.D(ifu_1_instr), .Q(register_3_q), .clk(Clk), .clr(Reset));  // open: en
  Controller controller_1 (
    .OpCode(register_3_q[31:26]), .Func(register_3_q[5:0]), .RegDst(RD), .ALUSrc(controller_1_alusrc),
    .MemtoReg(controller_1_memtoreg), .RegWrite(controller_1_regwrite), .MemWrite(controller_1_memwrite),
    .Branch(B), .ExtOp(EO), .ALUctr(controller_1_aluctr), .JEn(JEn), .jal(controller_1_jal), .Jr(Jr),
    .Byte(controller_1_byte), .Tnew(controller_1_tnew));  // open: SllEn, rsTuse, rtTuse
  Multiplexer #(.width(5)) multiplexer_2 (
    .in0(register_3_q[20:16]), .in1(register_3_q[15:11]), .out(multiplexer_2_out), .sel(RD));  // open: en
  Multiplexer #(.width(5)) multiplexer_3 (
    .in0(multiplexer_2_out), .in1({5{1'b1}}), .out(multiplexer_3_out), .sel(controller_1_jal));  // open: en
  GRF grf_1 (
    .WD(WD), .Reset(Reset), .Clk(Clk), .WE(RW), .A3(A3_W), .A1(register_3_q[25:21]),
    .A2(register_3_q[20:16]), .RD1(A), .RD2(grf_1_rd2));
  EXT ext_1 (.Imm16(register_3_q[15:0]), .ExtOp(EO), .out_3(ext_1_out_3));
  CU_E cu_e_1 (
    .in_2(controller_1_alusrc), .in_3(controller_1_memtoreg), .in_4(controller_1_regwrite),
    .in_5(controller_1_memwrite), .in_7(controller_1_aluctr), .in_8(controller_1_jal),
    .in_9(controller_1_byte), .out_12(cu_e_1_out_12), .out_13(cu_e_1_out_13), .out_14(cu_e_1_out_14),
    .out_15(cu_e_1_out_15), .out_17(cu_e_1_out_17), .out_18(cu_e_1_out_18), .out_19(cu_e_1_out_19),
    .out_20(cu_e_1_out_20), .in_10(controller_1_tnew));  // open: in_1, in_6, out_11, out_16
  Register #(.width(32)) register_4 (.D(register_1_q), .Q(register_4_q), .clk(Clk), .clr(Reset));  // open: en
  Register #(.width(32)) register_5 (.D(register_2_q), .Q(register_5_q), .clk(Clk), .clr(Reset));  // open: en
  Register #(.width(5)) register_6 (.D(multiplexer_3_out), .Q(register_6_q), .clk(Clk), .clr(Reset));  // open: en
  Register #(.width(32)) register_7 (.D(A), .Q(register_7_q), .clk(Clk), .clr(Reset));  // open: en
  Register #(.width(32)) register_8 (.D(grf_1_rd2), .Q(register_8_q), .clk(Clk), .clr(Reset));  // open: en
  Register #(.width(32)) register_9 (.D(ext_1_out_3), .Q(register_9_q), .clk(Clk), .clr(Reset));  // open: en
  Multiplexer #(.width(32)) multiplexer_4 (
    .in0(register_8_q), .in1(register_9_q), .out(multiplexer_4_out), .sel(cu_e_1_out_12));  // open: en
  ALU alu_1 (.SrcA(register_7_q), .SrcB(multiplexer_4_out), .ALUOp(cu_e_1_out_17), .ALUResult(alu_1_aluresult));
  CU_M cu_m_1 (
    .in_2(cu_e_1_out_13), .in_3(cu_e_1_out_14), .in_4(cu_e_1_out_15), .in_5(cu_e_1_out_18),
    .in_6(cu_e_1_out_19), .out_9(cu_m_1_out_9), .out_10(cu_m_1_out_10), .out_11(cu_m_1_out_11),
    .out_12(cu_m_1_out_12), .out_13(cu_m_1_out_13), .in_7(cu_e_1_out_20), .out_14(cu_m_1_out_14));  // open: in_1, out_8
  Register #(.width(32)) register_10 (.D(register_4_q), .Q(register_10_q), .clk(Clk), .clr(Reset));  // open: en
  Register #(.width(32)) register_11 (.D(register_5_q), .Q(register_11_q), .clk(Clk), .clr(Reset));  // open: en
  Register #(.width(5)) register_12 (.D(register_6_q), .Q(register_12_q), .clk(Clk), .clr(Reset));  // open: en
  Register #(.width(32)) register_13 (.D(alu_1_aluresult), .Q(register_13_q), .clk(Clk), .clr(Reset));  // open: en
  Register #(.width(32)) register_14 (.D(register_8_q), .Q(register_14_q), .clk(Clk), .clr(Reset));  // open: en
  \DM新  \dm新_1  (
    .A(register_13_q), .WD(register_14_q), .WE(cu_m_1_out_11), .D(\dm新_1_d ), .Clk(Clk), .in_4(Reset),
    .Byte(cu_m_1_out_13));
  CU_W cu_w_1 (
    .in_2(cu_m_1_out_9), .in_3(cu_m_1_out_10), .in_4(cu_m_1_out_12), .out_7(cu_w_1_out_7), .out_8(RW),
    .out_9(cu_w_1_out_9), .in_5(cu_m_1_out_14), .out_10(Tnew_W));  // open: in_1, out_6
  Register #(.width(32)) register_15 (.D(register_10_q), .Q(\输入到GRF ), .clk(Clk), .clr(Reset));  // open: en
  Register #(.width(32)) register_16 (.D(register_11_q), .Q(register_16_q), .clk(Clk), .clr(Reset));  // open: en
  Register #(.width(5)) register_17 (.D(register_12_q), .Q(A3_W), .clk(Clk), .clr(Reset));  // open: en
  Register #(.width(32)) register_18 (.D(register_13_q), .Q(register_18_q), .clk(Clk), .clr(Reset));  // open: en
  Register #(.width(32)) register_19 (.D(\dm新_1_d ), .Q(register_19_q), .clk(Clk), .clr(Reset));  // open: en
  Multiplexer #(.width(32)) multiplexer_5 (
    .in0(register_18_q), .in1(register_19_q), .out(multiplexer_5_out), .sel(cu_w_1_out_7));  // open: en
  Multiplexer #(.width(32)) multiplexer_6 (
    .in0(multiplexer_5_out), .in1(register_16_q), .out(WD), .sel(cu_w_1_out_9));  // open: en

  // Other names for the same wires on the sheet: Rst = Reset

  // Notes on the sheet:
  //   PC_D
  //   PC4_D
  //   Ins_D
  //   PC_E
  //   PC4_E
  //   A3_E
  //   RD1_E
  //   RD2_E
  //   EXT_E
  //   PC_M
  //   PC4_M
  //   A3_M
  //   aluR_M
  //   RD2_M
  //   PC_W
  //   PC4_W
  //   A3_W
  //   aluR_W
  //   dm_W
endmodule

module IFU (
  input  Clk,
  input  Reset,
  input  Branch,
  input  [31:0] BO,
  input  J,
  input  jr,
  input  [31:0] A,
  output [31:0] Instr,
  output [31:0] NPC,
  output [31:0] out_10
);

  wire [31:0] npc_1_npc;

  NPC npc_1 (.branch(Branch), .BOffset(BO), .pc(out_10), .npc(npc_1_npc), .J(J), .index(Instr[25:0]), .Jr(jr), .A(A));
  Register #(.width(32)) PC (.D(npc_1_npc), .Q(out_10), .clk(Clk), .clr(Reset));  // open: en
  IM im_1 (.PC(out_10), .Instr(Instr));
  Adder #(.width(32)) adder_1 (.a(out_10), .b(32'h4), .out(NPC));  // open: cin, cout

  // Other names for the same wires on the sheet: c = Clk; r = Reset
endmodule

module NPC (
  input  branch,
  input  [31:0] BOffset,
  input  [31:0] pc,
  input  [25:0] index,
  input  J,
  input  Jr,
  input  [31:0] A,
  output [31:0] npc
);

  wire [27:0] bit_extender_1_out, shifter_2_out;
  wire [31:0] adder_1_out, adder_2_out, multiplexer_1_out, multiplexer_2_out, shifter_1_out,
       subtractor_1_out, subtractor_2_out;

  assign bit_extender_1_out = {{2{1'b0}}, index};  // Bit_Extender bit_extender_1
  Shifter #(.width(32)) shifter_1 (.in(BOffset), .\dist (5'b00010), .out(shifter_1_out));
  Adder #(.width(32)) adder_1 (.a(pc), .b(32'h4), .out(adder_1_out));  // open: cin, cout
  Shifter #(.width(28)) shifter_2 (.in(bit_extender_1_out), .\dist (5'b00010), .out(shifter_2_out));
  Multiplexer #(.width(32)) multiplexer_1 (
    .in0({32{1'b0}}), .in1(shifter_1_out), .out(multiplexer_1_out), .sel(branch));  // open: en
  Subtractor #(.width(32)) subtractor_1 (.a(A), .b({32{1'b0}}), .out(subtractor_1_out));  // open: bin, bout
  // Probe on multiplexer_1_out
  Adder #(.width(32)) adder_2 (.a(multiplexer_1_out), .b(adder_1_out), .out(adder_2_out));  // open: cin, cout
  Subtractor #(.width(32)) subtractor_2 (
    .a({pc[31:28], shifter_2_out}), .b(32'h3000), .out(subtractor_2_out));  // open: bin, bout
  Multiplexer #(.width(32)) multiplexer_2 (
    .in0(adder_2_out), .in1(subtractor_2_out), .out(multiplexer_2_out), .sel(J));  // open: en
  Multiplexer #(.width(32)) multiplexer_3 (
    .in0(multiplexer_2_out), .in1(subtractor_1_out), .out(npc), .sel(Jr));  // open: en
endmodule

module IM (
  input  [31:0] PC,
  output [31:0] Instr
);

  wire comparator_1_eq, comparator_1_lt, or_1_out;
  wire [9:0] bit_extender_1_out;
  wire [31:0] rom_1_data, shifter_1_out;

  Shifter #(.width(32), .shift("ar")) shifter_1 (.in(PC), .\dist (5'b00010), .out(shifter_1_out));
  Bit_Extender #(.in_width(32), .out_width(10)) bit_extender_1 (.in(shifter_1_out), .out(bit_extender_1_out));
  Comparator #(.width(32), .mode("unsigned")) comparator_1 (
    .a(shifter_1_out), .b(32'h3fe), .eq(comparator_1_eq), .lt(comparator_1_lt));  // open: gt
  ROM #(.addrWidth(10), .dataWidth(32)) rom_1 (.addr(bit_extender_1_out), .data(rom_1_data));  // open: sel
  or or_1 (or_1_out, comparator_1_eq, comparator_1_lt);
  Multiplexer #(.width(32)) multiplexer_1 (
    .in0({32{1'b0}}), .in1(rom_1_data), .out(Instr), .sel(or_1_out));  // open: en

  // Notes on the sheet:
  //   contents of rom_1 (hex, n*v repeats v):
  //   20080000 20003cf2 85080 ad400000 21080001 200122f4 85080 214a0001 ad41ffff 214affff 21080001
  //   2002241a 85080 ad420000 21080001 20034418 85080 ad430000 21080001 200402fc 85080 ad440000 21080001
  //   20050e25 85080 ad450000 21080001 2006e7dd 85080 ad460000 21080001 20073110 85080 ad470000 21080001
  //   2009f62a 85080 ad490000 21080001 200ae4b6 85080 ad4a0000 21080001 200bf806 85080 ad4b0000 21080001
  //   200c186b 85080 ad4c0000 21080001 200d02af 85080 ad4d0000 21080001 200e1237 85080 ad4e0000 21080001
  //   200f2697 85080 ad4f0000 21080001 201056bf 85080 ad500000 21080001 20111bdd 85080 ad510000 21080001
  //   20123372 85080 ad520000 21080001 201340da 85080 ad530000 21080001 20144159 85080 ad540000 21080001
  //   20151620 85080 ad550000 21080001 2016e3b0 85080 ad560000 21080001 2017eb44 85080 ad570000 21080001
  //   201847ee 85080 ad580000 21080001 20194b2e 85080 ad590000 21080001 201a5b66 85080 ad5a0000 21080001
  //   201bebc9 85080 ad5b0000 21080001 201c0aad 85080 ad5c0000 21080001 201d4445 85080 ad5d0000 21080001
  //   201e0164 85080 ad5e0000 21080001 201f4644 85080 ad5f0000 21080001 c000c89 20130000 20090001 2699820
  //   85080 214a0001 a1530000 21080001 1133fff9 8000c9a 201003de 20110001 20090000 20120002 110602a
  //   1180000a 85080 3c01ffff 342bffff ad4b0000 1114020 2485004 1515822 ad4b0000 21080001 8000c8d 3e00008
endmodule

module Controller (
  input  [5:0] OpCode,
  input  [5:0] Func,
  output RegDst,
  output ALUSrc,
  output MemtoReg,
  output RegWrite,
  output MemWrite,
  output Branch,
  output JEn,
  output SllEn,
  output ExtOp,
  output [3:0] ALUctr,
  output jal,
  output Jr,
  output Byte,
  output [1:0] rsTuse,
  output [1:0] rtTuse,
  output [1:0] Tnew
);

  wire comparator_1_eq, \i或j译码_1_addi , \i或j译码_1_beq , \i或j译码_1_j , \i或j译码_1_jal , \i或j译码_1_lb ,
       \i或j译码_1_lui , \i或j译码_1_lw , \i或j译码_1_ori , \i或j译码_1_sb , \i或j译码_1_sw , jr_t, not_1_out, \r型译码_1_add ,
       \r型译码_1_sll , \r型译码_1_sllv , \r型译码_1_slt , \r型译码_1_sub ;

  Comparator #(.width(6), .mode("unsigned")) comparator_1 (
    .a(OpCode), .b({6{1'b0}}), .eq(comparator_1_eq));  // open: gt, lt
  not not_1 (not_1_out, comparator_1_eq);
  \R型译码  \r型译码_1  (
    .Func(Func), .En(comparator_1_eq), .add(\r型译码_1_add ), .sub(\r型译码_1_sub ), .sll(\r型译码_1_sll ),
    .sllv(\r型译码_1_sllv ), .slt(\r型译码_1_slt ), .jr(jr_t));
  \I或J译码  \i或j译码_1  (
    .OpCode(OpCode), .En(not_1_out), .beq(\i或j译码_1_beq ), .ori(\i或j译码_1_ori ), .lui(\i或j译码_1_lui ),
    .lw(\i或j译码_1_lw ), .sw(\i或j译码_1_sw ), .addi(\i或j译码_1_addi ), .j(\i或j译码_1_j ), .jal(\i或j译码_1_jal ),
    .sb(\i或j译码_1_sb ), .lb(\i或j译码_1_lb ));
  \或逻辑  \u_或逻辑_1  (
    .add(\r型译码_1_add ), .sub(\r型译码_1_sub ), .beq(\i或j译码_1_beq ), .ori(\i或j译码_1_ori ), .lui(\i或j译码_1_lui ),
    .lw(\i或j译码_1_lw ), .sw(\i或j译码_1_sw ), .RegDst(RegDst), .ALUSrc(ALUSrc), .MemtoReg(MemtoReg),
    .RegWrite(RegWrite), .MemWrite(MemWrite), .Branch(Branch), .ExtOp(ExtOp), .ALUctr_2(ALUctr[2]),
    .ALUctr_1(ALUctr[1]), .ALUctr_0(ALUctr[0]), .ALUctr_3(ALUctr[3]), .sll(\r型译码_1_sll ),
    .sllv(\r型译码_1_sllv ), .slt(\r型译码_1_slt ), .addi(\i或j译码_1_addi ), .j(\i或j译码_1_j ), .JEn(JEn),
    .SllEn(SllEn), .jal(\i或j译码_1_jal ), .jal_2(jal), .jr(jr_t), .jr_2(Jr), .Byte(Byte), .sb(\i或j译码_1_sb ),
    .lb(\i或j译码_1_lb ));

  assign rsTuse = 2'b11;
  assign rtTuse = 2'b11;
  assign Tnew = 2'b11;
endmodule

module \R型译码  (
  input  [5:0] Func,
  input  En,
  output add,
  output sub,
  output sll,
  output sllv,
  output slt,
  output jr
);

  wire decoder_1_out0, decoder_1_out1;

  Decoder #(.disabled(0)) decoder_1 (.out0(decoder_1_out0), .out1(decoder_1_out1), .sel(Func[5]), .en(En));
  Decoder #(.select(5), .disabled(0)) decoder_2 (
    .out0(sll), .out4(sllv), .out8(jr), .sel(Func[4:0]), .en(decoder_1_out0));  // open: out1, out2, out3, out5, out6, out7, out9, out10, out11, out12, out13, out14, out15, out16, out17, out18, out19, out20, out21, out22, out23, out24, out25, out26, out27, out28, out29, out30, out31
  Decoder #(.select(5), .disabled(0)) decoder_3 (
    .out0(add), .out2(sub), .out10(slt), .sel(Func[4:0]), .en(decoder_1_out1));  // open: out1, out3, out4, out5, out6, out7, out8, out9, out11, out12, out13, out14, out15, out16, out17, out18, out19, out20, out21, out22, out23, out24, out25, out26, out27, out28, out29, out30, out31
endmodule

module \I或J译码  (
  input  [5:0] OpCode,
  input  En,
  output beq,
  output ori,
  output lui,
  output lw,
  output sw,
  output addi,
  output j,
  output jal,
  output sb,
  output lb
);

  wire decoder_1_out0, decoder_1_out1, decoder_3_out6;

  Decoder #(.disabled(0)) decoder_1 (.out0(decoder_1_out0), .out1(decoder_1_out1), .sel(OpCode[5]), .en(En));
  Decoder #(.select(5), .disabled(0)) decoder_2 (
    .out2(j), .out3(jal), .out4(beq), .out8(addi), .out13(ori), .out15(lui), .sel(OpCode[4:0]),
    .en(decoder_1_out0));  // open: out0, out1, out5, out6, out7, out9, out10, out11, out12, out14, out16, out17, out18, out19, out20, out21, out22, out23, out24, out25, out26, out27, out28, out29, out30, out31
  Decoder #(.select(5), .disabled(0)) decoder_3 (
    .out0(lb), .out3(lw), .out6(decoder_3_out6), .out7(decoder_3_out6), .out8(sb), .out11(sw),
    .sel(OpCode[4:0]), .en(decoder_1_out1));  // open: out1, out2, out4, out5, out9, out10, out12, out13, out14, out15, out16, out17, out18, out19, out20, out21, out22, out23, out24, out25, out26, out27, out28, out29, out30, out31
endmodule

module \或逻辑  (
  input  add,
  input  sub,
  input  sll,
  input  sllv,
  input  slt,
  input  beq,
  input  ori,
  input  lui,
  input  lw,
  input  sw,
  input  addi,
  input  j,
  input  jal,
  input  jr,
  input  sb,
  input  lb,
  output RegDst,
  output ALUSrc,
  output MemtoReg,
  output RegWrite,
  output MemWrite,
  output Branch,
  output JEn,
  output SllEn,
  output ExtOp,
  output ALUctr_3,
  output ALUctr_2,
  output ALUctr_1,
  output ALUctr_0,
  output jal_2,
  output jr_2,
  output Byte
);

  or or_1 (RegDst, add, sub, sll, sllv, slt);
  or or_2 (ALUSrc, lb, ori, lui, lw, sw, addi, sb);
  or or_3 (MemtoReg, lw, lb);
  or or_4 (RegWrite, lb, addi, sllv, add, sub, ori, lui, lw, sll, slt, jal);
  or or_5 (MemWrite, sw, sb);
  buf or_6 (Branch, beq);  // OR_Gate
  or or_7 (JEn, j, jal);
  buf or_8 (SllEn, sll);  // OR_Gate
  or or_9 (ExtOp, beq, lw, sw, addi, sb, lb);
  or or_10 (ALUctr_3, sll, sllv, slt);
  or or_11 (ALUctr_2, sub, beq, lui);
  or or_12 (ALUctr_1, sllv, sll, add, sub, beq, lw, sw, addi, sb, lb);
  or or_13 (ALUctr_0, sllv, beq, ori, lui, slt, sll);
  buf or_14 (jal_2, jal);  // OR_Gate
  buf or_15 (jr_2, jr);  // OR_Gate
  or or_16 (Byte, sb, lb);
endmodule

module GRF (
  input  [31:0] WD,
  input  Clk,
  input  Reset,
  input  WE,
  input  [4:0] A3,
  input  [4:0] A1,
  input  [4:0] A2,
  output [31:0] RD1,
  output [31:0] RD2
);

  wire [31:0] _0, _1, _2, _3, _4, _5, _6, _7, _8, _9, _10, _11, _12, _13, _14, _15, _16, _17, _18, _19, _20,
       _21, _22, _23, _24, _25, _26, _27, _28, _29, _30, _31, demultiplexer_1_out0, demultiplexer_1_out1,
       demultiplexer_1_out2, demultiplexer_1_out3, demultiplexer_1_out4, demultiplexer_1_out5,
       demultiplexer_1_out6, demultiplexer_1_out7, demultiplexer_1_out8, demultiplexer_1_out9,
       demultiplexer_1_out10, demultiplexer_1_out11, demultiplexer_1_out12, demultiplexer_1_out13,
       demultiplexer_1_out14, demultiplexer_1_out15, demultiplexer_1_out16, demultiplexer_1_out17,
       demultiplexer_1_out18, demultiplexer_1_out19, demultiplexer_1_out20, demultiplexer_1_out21,
       demultiplexer_1_out22, demultiplexer_1_out23, demultiplexer_1_out24, demultiplexer_1_out25,
       demultiplexer_1_out26, demultiplexer_1_out27, demultiplexer_1_out28, demultiplexer_1_out29,
       demultiplexer_1_out30, demultiplexer_1_out31;

  Demultiplexer #(.select(5), .width(32), .tristate("true")) demultiplexer_1 (
    .out0(demultiplexer_1_out0), .out1(demultiplexer_1_out1), .out2(demultiplexer_1_out2),
    .out3(demultiplexer_1_out3), .out4(demultiplexer_1_out4), .out5(demultiplexer_1_out5),
    .out6(demultiplexer_1_out6), .out7(demultiplexer_1_out7), .out8(demultiplexer_1_out8),
    .out9(demultiplexer_1_out9), .out10(demultiplexer_1_out10), .out11(demultiplexer_1_out11),
    .out12(demultiplexer_1_out12), .out13(demultiplexer_1_out13), .out14(demultiplexer_1_out14),
    .out15(demultiplexer_1_out15), .out16(demultiplexer_1_out16), .out17(demultiplexer_1_out17),
    .out18(demultiplexer_1_out18), .out19(demultiplexer_1_out19), .out20(demultiplexer_1_out20),
    .out21(demultiplexer_1_out21), .out22(demultiplexer_1_out22), .out23(demultiplexer_1_out23),
    .out24(demultiplexer_1_out24), .out25(demultiplexer_1_out25), .out26(demultiplexer_1_out26),
    .out27(demultiplexer_1_out27), .out28(demultiplexer_1_out28), .out29(demultiplexer_1_out29),
    .out30(demultiplexer_1_out30), .out31(demultiplexer_1_out31), .in(WD), .sel(A3));  // open: en
  Register #(.width(32)) register_1 (.D(demultiplexer_1_out0), .Q(_0), .clk(Clk), .clr(1'b1));  // open: en
  Register #(.width(32)) register_2 (.D(demultiplexer_1_out4), .en(WE), .Q(_4), .clk(Clk), .clr(Reset));
  Register #(.width(32)) register_3 (.D(demultiplexer_1_out8), .en(WE), .Q(_8), .clk(Clk), .clr(Reset));
  Register #(.width(32)) register_4 (.D(demultiplexer_1_out12), .en(WE), .Q(_12), .clk(Clk), .clr(Reset));
  Register #(.width(32)) register_5 (.D(demultiplexer_1_out16), .en(WE), .Q(_16), .clk(Clk), .clr(Reset));
  Register #(.width(32)) register_6 (.D(demultiplexer_1_out20), .en(WE), .Q(_20), .clk(Clk), .clr(Reset));
  Register #(.width(32)) register_7 (.D(demultiplexer_1_out24), .en(WE), .Q(_24), .clk(Clk), .clr(Reset));
  Register #(.width(32)) register_8 (.D(demultiplexer_1_out28), .en(WE), .Q(_28), .clk(Clk), .clr(Reset));
  Register #(.width(32)) register_9 (.D(demultiplexer_1_out1), .en(WE), .Q(_1), .clk(Clk), .clr(Reset));
  Register #(.width(32)) register_10 (.D(demultiplexer_1_out5), .en(WE), .Q(_5), .clk(Clk), .clr(Reset));
  Register #(.width(32)) register_11 (.D(demultiplexer_1_out9), .en(WE), .Q(_9), .clk(Clk), .clr(Reset));
  Register #(.width(32)) register_12 (.D(demultiplexer_1_out13), .en(WE), .Q(_13), .clk(Clk), .clr(Reset));
  Register #(.width(32)) register_13 (.D(demultiplexer_1_out17), .en(WE), .Q(_17), .clk(Clk), .clr(Reset));
  Register #(.width(32)) register_14 (.D(demultiplexer_1_out21), .en(WE), .Q(_21), .clk(Clk), .clr(Reset));
  Register #(.width(32)) register_15 (.D(demultiplexer_1_out25), .en(WE), .Q(_25), .clk(Clk), .clr(Reset));
  Register #(.width(32)) register_16 (.D(demultiplexer_1_out29), .en(WE), .Q(_29), .clk(Clk), .clr(Reset));
  Register #(.width(32)) register_17 (.D(demultiplexer_1_out2), .en(WE), .Q(_2), .clk(Clk), .clr(Reset));
  Register #(.width(32)) register_18 (.D(demultiplexer_1_out6), .en(WE), .Q(_6), .clk(Clk), .clr(Reset));
  Register #(.width(32)) register_19 (.D(demultiplexer_1_out10), .en(WE), .Q(_10), .clk(Clk), .clr(Reset));
  Register #(.width(32)) register_20 (.D(demultiplexer_1_out14), .en(WE), .Q(_14), .clk(Clk), .clr(Reset));
  Register #(.width(32)) register_21 (.D(demultiplexer_1_out18), .en(WE), .Q(_18), .clk(Clk), .clr(Reset));
  Register #(.width(32)) register_22 (.D(demultiplexer_1_out22), .en(WE), .Q(_22), .clk(Clk), .clr(Reset));
  Register #(.width(32)) register_23 (.D(demultiplexer_1_out26), .en(WE), .Q(_26), .clk(Clk), .clr(Reset));
  Register #(.width(32)) register_24 (.D(demultiplexer_1_out30), .en(WE), .Q(_30), .clk(Clk), .clr(Reset));
  Register #(.width(32)) register_25 (.D(demultiplexer_1_out3), .en(WE), .Q(_3), .clk(Clk), .clr(Reset));
  Register #(.width(32)) register_26 (.D(demultiplexer_1_out7), .en(WE), .Q(_7), .clk(Clk), .clr(Reset));
  Register #(.width(32)) register_27 (.D(demultiplexer_1_out11), .en(WE), .Q(_11), .clk(Clk), .clr(Reset));
  Register #(.width(32)) register_28 (.D(demultiplexer_1_out15), .en(WE), .Q(_15), .clk(Clk), .clr(Reset));
  Register #(.width(32)) register_29 (.D(demultiplexer_1_out19), .en(WE), .Q(_19), .clk(Clk), .clr(Reset));
  Register #(.width(32)) register_30 (.D(demultiplexer_1_out23), .en(WE), .Q(_23), .clk(Clk), .clr(Reset));
  Register #(.width(32)) register_31 (.D(demultiplexer_1_out27), .en(WE), .Q(_27), .clk(Clk), .clr(Reset));
  Register #(.width(32)) register_32 (.D(demultiplexer_1_out31), .en(WE), .Q(_31), .clk(Clk), .clr(Reset));
  Multiplexer #(.select(5), .width(32)) multiplexer_1 (
    .in0(_0), .in1(_1), .in2(_2), .in3(_3), .in4(_4), .in5(_5), .in6(_6), .in7(_7), .in8(_8), .in9(_9),
    .in10(_10), .in11(_11), .in12(_12), .in13(_13), .in14(_14), .in15(_15), .in16(_16), .in17(_17),
    .in18(_18), .in19(_19), .in20(_20), .in21(_21), .in22(_22), .in23(_23), .in24(_24), .in25(_25),
    .in26(_26), .in27(_27), .in28(_28), .in29(_29), .in30(_30), .in31(_31), .out(RD1), .sel(A1));  // open: en
  Multiplexer #(.select(5), .width(32)) multiplexer_2 (
    .in0(_0), .in1(_1), .in2(_2), .in3(_3), .in4(_4), .in5(_5), .in6(_6), .in7(_7), .in8(_8), .in9(_9),
    .in10(_10), .in11(_11), .in12(_12), .in13(_13), .in14(_14), .in15(_15), .in16(_16), .in17(_17),
    .in18(_18), .in19(_19), .in20(_20), .in21(_21), .in22(_22), .in23(_23), .in24(_24), .in25(_25),
    .in26(_26), .in27(_27), .in28(_28), .in29(_29), .in30(_30), .in31(_31), .out(RD2), .sel(A2));  // open: en

  // Other names for the same wires on the sheet: en = WE; rst = Reset
endmodule

module ALU (
  input  [31:0] SrcA,
  input  [31:0] SrcB,
  input  [3:0] ALUOp,
  output [31:0] ALUResult
);

  wire comparator_1_eq, comparator_2_lt, comparator_3_gt;
  wire [4:0] bit_extender_1_out, bit_extender_2_out;
  wire [31:0] _0000, _0001, _0010, _0011, _0100, _0101, _0110, _0111, _1000, _1001, _1010, _1011, not_1_out,
       not_2_out, shifter_1_out, shifter_2_out, shifter_3_out;

  assign _0000 = SrcA & SrcB;  // AND_Gate and_1, 32 bits wide
  assign _0001 = SrcA | SrcB;  // OR_Gate or_1, 32 bits wide
  Adder #(.width(32)) adder_1 (.a(SrcA), .b(SrcB), .out(_0010));  // open: cin, cout
  assign not_1_out = ~SrcA;  // NOT_Gate not_1, 32 bits wide
  assign _0011 = not_1_out & SrcB;  // AND_Gate and_2, 32 bits wide
  assign _0100 = SrcA & not_2_out;  // AND_Gate and_3, 32 bits wide
  assign not_2_out = ~SrcB;  // NOT_Gate not_2, 32 bits wide
  Shifter #(.width(32)) shifter_1 (.in(SrcA), .\dist (5'b10000), .out(shifter_1_out));
  Shifter #(.width(32)) shifter_2 (.in(SrcB), .\dist (5'b10000), .out(shifter_2_out));
  Subtractor #(.width(32)) subtractor_1 (.a(SrcA), .b(SrcB), .out(_0110));  // open: bin, bout
  Comparator #(.width(32)) comparator_1 (.a(SrcA), .b(SrcB), .eq(comparator_1_eq));  // open: gt, lt
  Bit_Extender #(.in_width(32), .out_width(5)) bit_extender_1 (.in(SrcB), .out(bit_extender_1_out));
  Comparator #(.width(32)) comparator_2 (.a(SrcA), .b(SrcB), .lt(comparator_2_lt));  // open: gt, eq
  Comparator #(.width(32)) comparator_3 (.a(SrcA), .b(SrcB), .gt(comparator_3_gt));  // open: eq, lt
  Bit_Extender #(.in_width(32), .out_width(5)) bit_extender_2 (.in(SrcA), .out(bit_extender_2_out));
  Shifter #(.width(32), .shift("lr")) shifter_3 (.in(shifter_1_out), .\dist (5'b10000), .out(shifter_3_out));
  Shifter #(.width(32)) shifter_4 (.in(SrcA), .\dist (bit_extender_1_out), .out(_1000));
  Shifter #(.width(32)) shifter_5 (.in(SrcB), .\dist (bit_extender_2_out), .out(_1011));
  assign _0101 = shifter_3_out | shifter_2_out;  // OR_Gate or_2, 32 bits wide
  assign _0111 = {{31{1'b0}}, comparator_1_eq};  // Bit_Extender bit_extender_3
  assign _1001 = {{31{1'b0}}, comparator_2_lt};  // Bit_Extender bit_extender_4
  assign _1010 = {{31{1'b0}}, comparator_3_gt};  // Bit_Extender bit_extender_5
  Multiplexer #(.select(4), .width(32)) multiplexer_1 (
    .in0(_0000), .in1(_0001), .in2(_0010), .in3(_0011), .in4(_0100), .in5(_0101), .in6(_0110), .in7(_0111),
    .in8(_1000), .in9(_1001), .in10(_1010), .in11(_1011), .out(ALUResult), .sel(ALUOp));  // open: in12, in13, in14, in15, en

  // Other names for the same wires on the sheet: A[31:0] = SrcA; B[31:0] = SrcB
endmodule

module DM (
  input  [31:0] A,
  input  [31:0] WD,
  input  WE,
  input  \byte ,
  input  Clk,
  input  Rst,
  output [31:0] D
);

  wire s0, s1, s2, s3;
  wire [7:0] d0_t, D1, d1_t, D2, d2_t, D3, d3_t, multiplexer_4_out;
  wire [9:0] A_t;
  wire [31:0] bit_extender_2_out, shifter_1_out;

  Shifter #(.width(32), .shift("lr")) shifter_1 (.in(A), .\dist (5'b00010), .out(shifter_1_out));
  Multiplexer #(.width(8)) multiplexer_1 (.in0(WD[15:8]), .in1(WD[7:0]), .out(D1), .sel(\byte ));  // open: en
  Multiplexer #(.width(8)) multiplexer_2 (.in0(WD[23:16]), .in1(WD[7:0]), .out(D2), .sel(\byte ));  // open: en
  Multiplexer #(.width(8)) multiplexer_3 (.in0(WD[31:24]), .in1(WD[7:0]), .out(D3), .sel(\byte ));  // open: en
  Decoder #(.select(2)) decoder_1 (.out0(s0), .out1(s1), .out2(s2), .out3(s3), .sel(A[1:0]), .en(\byte ));
  Bit_Extender #(.in_width(32), .out_width(10)) bit_extender_1 (.in(shifter_1_out), .out(A_t));
  RAM #(.addrWidth(10), .bus("separate")) ram_1 (
    .addr(A_t), .din(WD[7:0]), .data(d0_t), .str(WE), .sel(s0), .clk(Clk), .clr(Rst));  // open: ld
  RAM #(.addrWidth(10), .bus("separate")) ram_2 (
    .addr(A_t), .din(D2), .data(d2_t), .str(WE), .sel(s2), .clk(Clk), .clr(Rst));  // open: ld
  RAM #(.addrWidth(10), .bus("separate")) ram_3 (
    .addr(A_t), .din(D1), .data(d1_t), .str(WE), .sel(s1), .clk(Clk), .clr(Rst));  // open: ld
  RAM #(.addrWidth(10), .bus("separate")) ram_4 (
    .addr(A_t), .din(D3), .data(d3_t), .str(WE), .sel(s3), .clk(Clk), .clr(Rst));  // open: ld
  Multiplexer #(.select(2), .width(8)) multiplexer_4 (
    .in0(d0_t), .in1(d1_t), .in2(d2_t), .in3(d3_t), .out(multiplexer_4_out), .sel(A[1:0]));  // open: en
  assign bit_extender_2_out = {{24{1'b0}}, multiplexer_4_out};  // Bit_Extender bit_extender_2
  Multiplexer #(.width(32)) multiplexer_5 (
    .in0({d3_t, d2_t, d1_t, d0_t}), .in1(bit_extender_2_out), .out(D), .sel(\byte ));  // open: en

  // Other names for the same wires on the sheet: a_t_t[1:0] = A[1:0]; b = \byte ; D0[7:0] = WD[7:0]
endmodule

module EXT (
  input  [15:0] Imm16,
  input  ExtOp,
  output [31:0] out_3
);

  wire [31:0] bit_extender_1_out, bit_extender_2_out;

  assign bit_extender_1_out = {{16{1'b0}}, Imm16};  // Bit_Extender bit_extender_1
  assign bit_extender_2_out = {{16{Imm16[15]}}, Imm16};  // Bit_Extender bit_extender_2
  Multiplexer #(.width(32)) multiplexer_1 (
    .in0(bit_extender_1_out), .in1(bit_extender_2_out), .out(out_3), .sel(ExtOp));  // open: en
endmodule

module \DM新  (
  input  [31:0] A,
  input  [31:0] WD,
  input  Clk,
  input  in_4,
  input  WE,
  input  Byte,
  output [31:0] D
);

  wire [4:0] bit_extender_1_out, bit_extender_2_out, shifter_2_out, shifter_3_out;
  wire [7:0] multiplexer_1_out;
  wire [9:0] bit_extender_3_out;
  wire [31:0] and_1_out, bit_extender_4_out, D_t, or_1_out, ram_1_data, shifter_1_out, shifter_4_out,
       shifter_5_out, xor_1_out;

  assign bit_extender_1_out = {{3{1'b0}}, A[1:0]};  // Bit_Extender bit_extender_1
  assign bit_extender_2_out = {{3{1'b0}}, A[1:0]};  // Bit_Extender bit_extender_2
  Shifter #(.width(32), .shift("lr")) shifter_1 (.in(A), .\dist (5'b00010), .out(shifter_1_out));
  Shifter #(.width(5)) shifter_2 (.in(bit_extender_1_out), .\dist (3'b011), .out(shifter_2_out));
  Shifter #(.width(5)) shifter_3 (.in(bit_extender_2_out), .\dist (3'b011), .out(shifter_3_out));
  Bit_Extender #(.in_width(32), .out_width(10)) bit_extender_3 (.in(shifter_1_out), .out(bit_extender_3_out));
  Shifter #(.width(32)) shifter_4 (.in(WD), .\dist (shifter_2_out), .out(shifter_4_out));
  Shifter #(.width(32)) shifter_5 (.in(32'hff), .\dist (shifter_3_out), .out(shifter_5_out));
  assign xor_1_out = {32{1'b1}} ^ shifter_5_out;  // XOR_Gate xor_1, 32 bits wide
  RAM #(.addrWidth(10), .dataWidth(32), .bus("separate")) ram_1 (
    .addr(bit_extender_3_out), .din(D_t), .data(ram_1_data), .str(WE), .clk(Clk), .clr(in_4));  // open: sel, ld
  assign and_1_out = ram_1_data & xor_1_out;  // AND_Gate and_1, 32 bits wide
  Multiplexer #(.select(2), .width(8)) multiplexer_1 (
    .in0(ram_1_data[7:0]), .in1(ram_1_data[15:8]), .in2(ram_1_data[23:16]), .in3(ram_1_data[31:24]),
    .out(multiplexer_1_out), .sel(A[1:0]));  // open: en
  assign or_1_out = shifter_4_out | and_1_out;  // OR_Gate or_1, 32 bits wide
  assign bit_extender_4_out = {{24{1'b0}}, multiplexer_1_out};  // Bit_Extender bit_extender_4
  Multiplexer #(.width(32)) multiplexer_2 (.in0(WD), .in1(or_1_out), .out(D_t), .sel(Byte));  // open: en
  Multiplexer #(.width(32)) multiplexer_3 (
    .in0(ram_1_data), .in1(bit_extender_4_out), .out(D), .sel(Byte));  // open: en

  // Other names for the same wires on the sheet: a_t[1:0] = A[1:0]
endmodule

module CU_E (
  input  in_1,
  input  in_2,
  input  in_3,
  input  in_4,
  input  in_5,
  input  in_6,
  input  [3:0] in_7,
  input  in_8,
  input  in_9,
  input  [1:0] in_10,
  output out_11,
  output out_12,
  output out_13,
  output out_14,
  output out_15,
  output out_16,
  output [3:0] out_17,
  output out_18,
  output out_19,
  output [1:0] out_20
);


  assign out_11 = in_1;
  assign out_12 = in_2;
  assign out_13 = in_3;
  assign out_14 = in_4;
  assign out_15 = in_5;
  assign out_16 = in_6;
  assign out_17 = in_7;
  assign out_18 = in_8;
  assign out_19 = in_9;
  assign out_20 = in_10;
endmodule

module CU_M (
  input  in_1,
  input  in_2,
  input  in_3,
  input  in_4,
  input  in_5,
  input  in_6,
  input  [1:0] in_7,
  output out_8,
  output out_9,
  output out_10,
  output out_11,
  output out_12,
  output out_13,
  output [1:0] out_14
);


  assign out_8 = in_1;
  assign out_9 = in_2;
  assign out_10 = in_3;
  assign out_11 = in_4;
  assign out_12 = in_5;
  assign out_13 = in_6;
  assign out_14 = in_7;
endmodule

module CU_W (
  input  in_1,
  input  in_2,
  input  in_3,
  input  in_4,
  input  [1:0] in_5,
  output out_6,
  output out_7,
  output out_8,
  output out_9,
  output [1:0] out_10
);


  assign out_6 = in_1;
  assign out_7 = in_2;
  assign out_8 = in_3;
  assign out_9 = in_4;
  assign out_10 = in_5;
endmodule
