// Logisim project 2^n mod 5.circ as structural Verilog: 2 circuits, main circuit mod5
module mod5 (
  input  In,
  output S0,
  output S1,
  output S2,
  output S3,
  output S4
);

  wire clock_1_out;
  wire [1:0] register_1_q, state_change_1_next_state0;

  state_change state_change_1 (
    .In(In), .state1(register_1_q[1]), .state0(register_1_q[0]), .next_state1(state_change_1_next_state0[1]),
    .next_state0(state_change_1_next_state0[0]));
  Clock clock_1 (.out(clock_1_out));
  Register #(.width(2)) register_1 (
    .D(state_change_1_next_state0), .Q(register_1_q), .clk(clock_1_out));  // open: en, clr
  and and_1 (S0, 1'b0, In);
  Decoder #(.select(2)) decoder_1 (
    .out0(S1), .out1(S2), .out2(S3), .out3(S4), .sel(state_change_1_next_state0));  // open: en
endmodule

module state_change (
  input  In,
  input  state1,
  input  state0,
  output next_state1,
  output next_state0
);

  wire and_1_out, and_2_out, and_3_out, and_4_out, and_5_out, and_6_out, not_1_out, not_2_out, not_3_out,
       not_4_out, not_5_out, not_6_out, not_7_out, not_8_out;

  not not_1 (not_1_out, state1);
  not not_2 (not_2_out, state0);
  not not_3 (not_3_out, In);
  not not_4 (not_4_out, state1);
  not not_5 (not_5_out, In);
  not not_6 (not_6_out, state0);
  not not_7 (not_7_out, state1);
  not not_8 (not_8_out, state0);
  and and_1 (and_1_out, not_1_out, state0);
  and and_2 (and_2_out, state1, not_2_out);
  and and_3 (and_3_out, not_3_out, not_4_out, state0);
  and and_4 (and_4_out, not_5_out, state1, not_6_out);
  and and_5 (and_5_out, In, not_7_out, not_8_out);
  and and_6 (and_6_out, In, state1, state0);
  or or_1 (next_state1, and_1_out, and_2_out);
  or or_2 (next_state0, and_3_out, and_4_out, and_5_out, and_6_out);
endmodule
