// Logisim project 斐波那契数列.circ as structural Verilog: 1 circuit, main circuit main
module main (
  input  [2:0] N,
  output [3:0] out_2
);

  wire CLK, comparator_1_eq, comparator_1_lt, counter_1_q, not_1_out, or_1_out;
  wire [2:0] counter_2_q;
  wire [3:0] adder_1_out, multiplexer_1_out, register_1_q, register_2_q;

  Clock clock_1 (.out(CLK));
  Counter #(.width(1), .max('h1), .ongoal("stay")) counter_1 (
    .Q(counter_1_q), .clk(CLK));  // open: load, D, count, carry, clr
  Counter #(.width(3), .max('h7), .ongoal("stay")) counter_2 (
    .Q(counter_2_q), .clk(CLK));  // open: load, D, count, carry, clr
  Multiplexer #(.width(4)) multiplexer_1 (
    .in0(4'b0001), .in1(register_2_q), .out(multiplexer_1_out), .sel(counter_1_q));  // open: en
  Comparator #(.width(3), .mode("unsigned")) comparator_1 (
    .a(N), .b(counter_2_q), .eq(comparator_1_eq), .lt(comparator_1_lt));  // open: gt
  Register #(.width(4)) register_1 (.D(multiplexer_1_out), .en(not_1_out), .Q(register_1_q), .clk(CLK));  // open: clr
  Adder #(.width(4)) adder_1 (.a(register_1_q), .b(register_2_q), .out(adder_1_out));  // open: cin, cout
  not not_1 (not_1_out, or_1_out);
  or or_1 (or_1_out, comparator_1_eq, comparator_1_lt);
  Register #(.width(4)) register_2 (.D(adder_1_out), .en(not_1_out), .Q(register_2_q), .clk(CLK));  // open: clr
  Multiplexer #(.width(4)) multiplexer_2 (.in0(4'b0000), .in1(adder_1_out), .out(out_2), .sel(or_1_out));  // open: en
endmodule
