// Logisim project 斐波那契数列（矩阵快速幂）.circ as structural Verilog: 3 circuits, main circuit main
module main (
  input  [31:0] N,
  output [31:0] Nth
);

  wire CLK, comparator_1_lt, counter_1_q, counter_2_q, counter_4_q, counter_5_q, counter_6_q, counter_7_q,
       counter_8_q, counter_9_q, multiplexer_3_out, stop;
  wire [4:0] bit_extender_1_out, bitfinder_1_index;
  wire [5:0] bit_extender_2_out, counter_3_q;
  wire [31:0] A, A1, A2, A2_star, A_star, B, B1, B2, B2_star, B_star, C, C1, C2_star, C_star, D, D1, D2,
       D2_star, D_star, \矩阵乘法_1_a , \矩阵乘法_1_b , \矩阵乘法_1_c , \矩阵乘法_1_d , \矩阵平方_1_a1 , \矩阵平方_1_b1 ,
       \矩阵平方_1_c1 , \矩阵平方_1_d1 ;

  Clock clock_1 (.out(CLK));
  Multiplexer #(.width(32)) multiplexer_1 (.in0(32'h1), .in1(A_star), .out(A), .sel(counter_1_q));  // open: en
  Counter #(.width(1), .max('h1), .ongoal("stay")) counter_1 (
    .Q(counter_1_q), .clk(CLK));  // open: load, D, count, carry, clr
  Multiplexer #(.width(32)) multiplexer_2 (.in0(32'h1), .in1(A2_star), .out(A2), .sel(counter_2_q));  // open: en
  Counter #(.width(1), .max('h1), .ongoal("stay")) counter_2 (
    .Q(counter_2_q), .clk(CLK));  // open: load, D, count, carry, clr
  Counter #(.width(6), .max('h20), .ongoal("stay")) counter_3 (
    .Q(counter_3_q), .clk(CLK));  // open: load, D, count, carry, clr
  Multiplexer #(.select(5)) multiplexer_3 (
    .in0(N[0]), .in1(N[1]), .in2(N[2]), .in3(N[3]), .in4(N[4]), .in5(N[5]), .in6(N[6]), .in7(N[7]),
    .in8(N[8]), .in9(N[9]), .in10(N[10]), .in11(N[11]), .in12(N[12]), .in13(N[13]), .in14(N[14]),
    .in15(N[15]), .in16(N[16]), .in17(N[17]), .in18(N[18]), .in19(N[19]), .in20(N[20]), .in21(N[21]),
    .in22(N[22]), .in23(N[23]), .in24(N[24]), .in25(N[25]), .in26(N[26]), .in27(N[27]), .in28(N[28]),
    .in29(N[29]), .in30(N[30]), .in31(N[31]), .out(multiplexer_3_out), .sel(bit_extender_1_out));  // open: en
  Bit_Extender #(.in_width(6), .out_width(5)) bit_extender_1 (.in(counter_3_q), .out(bit_extender_1_out));
  Multiplexer #(.width(32)) multiplexer_4 (.in0(32'h1), .in1(B_star), .out(B), .sel(counter_4_q));  // open: en
  Counter #(.width(1), .max('h1), .ongoal("stay")) counter_4 (
    .Q(counter_4_q), .clk(CLK));  // open: load, D, count, carry, clr
  Multiplexer #(.width(32)) multiplexer_5 (.in0({32{1'b0}}), .in1(B2_star), .out(B2), .sel(counter_5_q));  // open: en
  Counter #(.width(1), .max('h1), .ongoal("stay")) counter_5 (
    .Q(counter_5_q), .clk(CLK));  // open: load, D, count, carry, clr
  \矩阵平方  \u_矩阵平方_1  (
    .A(A), .B(B), .C(C), .D(D), .A1(\矩阵平方_1_a1 ), .B1(\矩阵平方_1_b1 ), .C1(\矩阵平方_1_c1 ), .D1(\矩阵平方_1_d1 ));
  Multiplexer #(.width(32)) multiplexer_6 (.in0(32'h1), .in1(A), .out(A1), .sel(multiplexer_3_out));  // open: en
  Multiplexer #(.width(32)) multiplexer_7 (.in0({32{1'b0}}), .in1(B), .out(B1), .sel(multiplexer_3_out));  // open: en
  Multiplexer #(.width(32)) multiplexer_8 (.in0({32{1'b0}}), .in1(C), .out(C1), .sel(multiplexer_3_out));  // open: en
  Multiplexer #(.width(32)) multiplexer_9 (.in0(32'h1), .in1(D), .out(D1), .sel(multiplexer_3_out));  // open: en
  BitFinder #(.width(32), .\type ("high1")) bitfinder_1 (.in(N), .index(bitfinder_1_index));  // open: found
  Multiplexer #(.width(32)) multiplexer_10 (.in0(32'h1), .in1(C_star), .out(C), .sel(counter_6_q));  // open: en
  Counter #(.width(1), .max('h1), .ongoal("stay")) counter_6 (
    .Q(counter_6_q), .clk(CLK));  // open: load, D, count, carry, clr
  Multiplexer #(.width(32)) multiplexer_11 (.in0({32{1'b0}}), .in1(C2_star), .out(B2), .sel(counter_7_q));  // open: en
  Counter #(.width(1), .max('h1), .ongoal("stay")) counter_7 (
    .Q(counter_7_q), .clk(CLK));  // open: load, D, count, carry, clr
  Register #(.width(32)) register_1 (.D(\矩阵平方_1_a1 ), .en(stop), .Q(A_star), .clk(CLK));  // open: clr
  Register #(.width(32)) register_2 (.D(\矩阵平方_1_b1 ), .en(stop), .Q(B_star), .clk(CLK));  // open: clr
  Register #(.width(32)) register_3 (.D(\矩阵平方_1_c1 ), .en(stop), .Q(C_star), .clk(CLK));  // open: clr
  Register #(.width(32)) register_4 (.D(\矩阵平方_1_d1 ), .en(stop), .Q(D_star), .clk(CLK));  // open: clr
  assign bit_extender_2_out = {{1{1'b0}}, bitfinder_1_index};  // Bit_Extender bit_extender_2
  Comparator #(.width(6), .mode("unsigned")) comparator_1 (
    .a(bit_extender_2_out), .b(counter_3_q), .lt(comparator_1_lt));  // open: gt, eq
  Counter #(.width(1), .max('h1), .ongoal("stay")) counter_8 (
    .Q(counter_8_q), .clk(CLK));  // open: load, D, count, carry, clr
  Counter #(.width(1), .max('h1), .ongoal("stay")) counter_9 (
    .Q(counter_9_q), .clk(CLK));  // open: load, D, count, carry, clr
  Multiplexer #(.width(32)) multiplexer_12 (.in0({32{1'b0}}), .in1(D_star), .out(D), .sel(counter_8_q));  // open: en
  Multiplexer #(.width(32)) multiplexer_13 (.in0(32'h1), .in1(D2_star), .out(D2), .sel(counter_9_q));  // open: en
  \矩阵乘法  \u_矩阵乘法_1  (
    .A1(A1), .B1(B1), .C1(C1), .D1(D1), .A2(A2), .B2(B2), .C2(B2), .D2(D2), .A(\矩阵乘法_1_a ), .B(\矩阵乘法_1_b ),
    .C(\矩阵乘法_1_c ), .D(\矩阵乘法_1_d ));
  Multiplexer #(.width(32)) multiplexer_14 (
    .in0({32{1'b0}}), .in1(B2_star), .out(Nth), .sel(comparator_1_lt));  // open: en
  not not_1 (stop, comparator_1_lt);
  Register #(.width(32)) register_5 (.D(\矩阵乘法_1_a ), .en(stop), .Q(A2_star), .clk(CLK));  // open: clr
  Register #(.width(32)) register_6 (.D(\矩阵乘法_1_b ), .en(stop), .Q(B2_star), .clk(CLK));  // open: clr
  Register #(.width(32)) register_7 (.D(\矩阵乘法_1_c ), .en(stop), .Q(C2_star), .clk(CLK));  // open: clr
  Register #(.width(32)) register_8 (.D(\矩阵乘法_1_d ), .en(stop), .Q(D2_star), .clk(CLK));  // open: clr

  // Other names for the same wires on the sheet: A_star_star[31:0] = A; B_star_star[31:0] = B; C2[31:0] = B2;
  //   C_star_star[31:0] = C; D_star_star[31:0] = D
endmodule

module \矩阵平方  (
  input  [31:0] A,
  input  [31:0] B,
  input  [31:0] C,
  input  [31:0] D,
  output [31:0] A1,
  output [31:0] B1,
  output [31:0] C1,
  output [31:0] D1
);

  wire [31:0] multiplier_1_out, multiplier_2_out, multiplier_3_out, multiplier_4_out, multiplier_5_out,
       multiplier_6_out, multiplier_7_out, multiplier_8_out;

  Multiplier #(.width(32)) multiplier_1 (.a(A), .b(A), .out(multiplier_1_out));  // open: cin, cout
  Multiplier #(.width(32)) multiplier_2 (.a(B), .b(C), .out(multiplier_2_out));  // open: cin, cout
  Multiplier #(.width(32)) multiplier_3 (.a(A), .b(B), .out(multiplier_3_out));  // open: cin, cout
  Multiplier #(.width(32)) multiplier_4 (.a(B), .b(D), .out(multiplier_4_out));  // open: cin, cout
  Multiplier #(.width(32)) multiplier_5 (.a(C), .b(A), .out(multiplier_5_out));  // open: cin, cout
  Multiplier #(.width(32)) multiplier_6 (.a(C), .b(D), .out(multiplier_6_out));  // open: cin, cout
  Multiplier #(.width(32)) multiplier_7 (.a(B), .b(C), .out(multiplier_7_out));  // open: cin, cout
  Multiplier #(.width(32)) multiplier_8 (.a(D), .b(D), .out(multiplier_8_out));  // open: cin, cout
  Adder #(.width(32)) adder_1 (.a(multiplier_1_out), .b(multiplier_2_out), .out(A1));  // open: cin, cout
  Adder #(.width(32)) adder_2 (.a(multiplier_3_out), .b(multiplier_4_out), .out(B1));  // open: cin, cout
  Adder #(.width(32)) adder_3 (.a(multiplier_5_out), .b(multiplier_6_out), .out(C1));  // open: cin, cout
  Adder #(.width(32)) adder_4 (.a(multiplier_7_out), .b(multiplier_8_out), .out(D1));  // open: cin, cout
endmodule

module \矩阵乘法  (
  input  [31:0] A1,
  input  [31:0] B1,
  input  [31:0] C1,
  input  [31:0] D1,
  input  [31:0] A2,
  input  [31:0] B2,
  input  [31:0] C2,
  input  [31:0] D2,
  output [31:0] A,
  output [31:0] B,
  output [31:0] C,
  output [31:0] D
);

  wire [31:0] multiplier_1_out, multiplier_2_out, multiplier_3_out, multiplier_4_out, multiplier_5_out,
       multiplier_6_out, multiplier_7_out, multiplier_8_out;

  Multiplier #(.width(32)) multiplier_1 (.a(A1), .b(A2), .out(multiplier_1_out));  // open: cin, cout
  Multiplier #(.width(32)) multiplier_2 (.a(B1), .b(C2), .out(multiplier_2_out));  // open: cin, cout
  Multiplier #(.width(32)) multiplier_3 (.a(A1), .b(B2), .out(multiplier_3_out));  // open: cin, cout
  Multiplier #(.width(32)) multiplier_4 (.a(B1), .b(D2), .out(multiplier_4_out));  // open: cin, cout
  Multiplier #(.width(32)) multiplier_5 (.a(C1), .b(A2), .out(multiplier_5_out));  // open: cin, cout
  Multiplier #(.width(32)) multiplier_6 (.a(D1), .b(C2), .out(multiplier_6_out));  // open: cin, cout
  Multiplier #(.width(32)) multiplier_7 (.a(C1), .b(B2), .out(multiplier_7_out));  // open: cin, cout
  Multiplier #(.width(32)) multiplier_8 (.a(D1), .b(D2), .out(multiplier_8_out));  // open: cin, cout
  Adder #(.width(32)) adder_1 (.a(multiplier_1_out), .b(multiplier_2_out), .out(A));  // open: cin, cout
  Adder #(.width(32)) adder_2 (.a(multiplier_3_out), .b(multiplier_4_out), .out(B));  // open: cin, cout
  Adder #(.width(32)) adder_3 (.a(multiplier_5_out), .b(multiplier_6_out), .out(C));  // open: cin, cout
  Adder #(.width(32)) adder_4 (.a(multiplier_7_out), .b(multiplier_8_out), .out(D));  // open: cin, cout
endmodule
