// Logisim project CRC.circ as structural Verilog: 2 circuits, main circuit CRC
module CRC (
  input  [7:0] A,
  input  [3:0] B,
  output [10:0] C
);

  wire [2:0] div_1_c, div_2_c, div_3_c, div_4_c, div_5_c, div_6_c;
  wire [3:1] div_7_c;
  wire [10:0] bit_extender_1_out, shifter_1_out;

  assign bit_extender_1_out = {{3{1'b0}}, A};  // Bit_Extender bit_extender_1
  // Probe on shifter_1_out
  Shifter #(.width(11)) shifter_1 (.in(bit_extender_1_out), .\dist (4'b0011), .out(shifter_1_out));
  div div_1 (.A(shifter_1_out[10:7]), .B(B), .C(div_1_c));  // open: D
  div div_2 (.A({div_7_c, shifter_1_out[4]}), .B(B), .C(div_2_c));  // open: D
  div div_3 (.A({div_1_c, shifter_1_out[6]}), .B(B), .C(div_3_c));  // open: D
  div div_4 (.A({div_2_c, shifter_1_out[3]}), .B(B), .C(div_4_c));  // open: D
  div div_5 (.A({div_6_c, shifter_1_out[1]}), .B(B), .C(div_5_c));  // open: D
  div div_6 (.A({div_4_c, shifter_1_out[2]}), .B(B), .C(div_6_c));  // open: D
  div div_7 (.A({div_3_c, shifter_1_out[5]}), .B(B), .C(div_7_c));  // open: D
  div div_8 (.A({div_5_c, shifter_1_out[0]}), .B(B), .C(C[2:0]));  // open: D

  assign C[10:3] = A;
endmodule

module div (
  input  [3:0] A,
  input  [3:0] B,
  output D,
  output [2:0] C
);

  wire [3:0] multiplexer_1_out, xor_1_out;

  Multiplexer #(.width(4)) multiplexer_1 (.in0(4'b0000), .in1(B), .out(multiplexer_1_out), .sel(A[3]));  // open: en
  assign xor_1_out = A ^ multiplexer_1_out;  // XOR_Gate xor_1, 4 bits wide
  Bit_Extender #(.in_width(4), .out_width(3)) bit_extender_1 (.in(xor_1_out), .out(C));

  assign D = A[3];
endmodule
