// Logisim project fsm.circ as structural Verilog: 3 circuits, main circuit fsm
module fsm (
  input  CLR,
  input  [1:0] In,
  output Z
);

  wire clock_1_out, not_1_out;
  wire [1:0] register_1_q, tran_1_n0;

  not not_1 (not_1_out, CLR);
  \tran  tran_1 (
    .CLR(not_1_out), .In1(In[1]), .In0(In[0]), .s1(register_1_q[1]), .s0(register_1_q[0]), .N1(tran_1_n0[1]),
    .n0(tran_1_n0[0]));
  Register #(.width(2)) register_1 (.D(tran_1_n0), .Q(register_1_q), .clk(clock_1_out));  // open: en, clr
  Clock clock_1 (.out(clock_1_out));
  out out_1 (.in1(In[1]), .in0(In[0]), .s1(register_1_q[1]), .s0(register_1_q[0]), .Z(Z));
endmodule

module \tran  (
  input  CLR,
  input  In1,
  input  In0,
  input  s1,
  input  s0,
  output N1,
  output n0
);

  wire and_1_out, and_2_out, and_3_out, and_4_out, and_5_out, and_6_out, and_7_out, not_1_out, not_2_out,
       not_3_out, not_4_out, not_5_out, not_6_out, not_7_out, not_8_out, not_9_out, not_10_out, not_11_out,
       not_12_out, not_13_out;

  not not_1 (not_1_out, In1);
  not not_2 (not_2_out, s1);
  not not_3 (not_3_out, In0);
  not not_4 (not_4_out, s1);
  not not_5 (not_5_out, In0);
  not not_6 (not_6_out, s0);
  not not_7 (not_7_out, In0);
  not not_8 (not_8_out, s1);
  not not_9 (not_9_out, In0);
  not not_10 (not_10_out, s0);
  not not_11 (not_11_out, In1);
  not not_12 (not_12_out, s0);
  not not_13 (not_13_out, In1);
  and and_1 (and_1_out, CLR, not_1_out, not_2_out, s0);
  and and_2 (and_2_out, CLR, not_3_out, not_4_out, s0);
  and and_3 (and_3_out, CLR, not_5_out, s1, not_6_out);
  and and_4 (and_4_out, CLR, not_7_out, not_8_out, s0);
  and and_5 (and_5_out, CLR, not_9_out, s1, not_10_out);
  and and_6 (and_6_out, CLR, not_11_out, In0, not_12_out);
  and and_7 (and_7_out, CLR, not_13_out, In0, s1);
  or or_1 (N1, and_1_out, and_2_out, and_3_out);
  or or_2 (n0, and_4_out, and_5_out, and_6_out, and_7_out);
endmodule

module out (
  input  in1,
  input  in0,
  input  s1,
  input  s0,
  output Z
);

  wire not_1_out;

  not not_1 (not_1_out, in0);
  and and_1 (Z, not_1_out, s1, s0);
endmodule
