// Logisim project ftoi.circ as structural Verilog: 1 circuit, main circuit ftoi
module ftoi (
  input  [15:0] float,
  output [31:0] \int 
);

  wire comparator_1_eq, comparator_2_eq, comparator_3_lt, or_1_out;
  wire [4:0] negator_1_out, xor_1_out;
  wire [10:0] bit_extender_1_out;
  wire [31:0] bit_extender_2_out, multiplexer_1_out, negator_2_out, shifter_1_out, shifter_2_out;

  assign bit_extender_1_out = {{1{1'b1}}, float[9:0]};  // Bit_Extender bit_extender_1
  assign bit_extender_2_out = {{21{1'b0}}, bit_extender_1_out};  // Bit_Extender bit_extender_2
  Comparator #(.width(5), .mode("unsigned")) comparator_1 (
    .a(float[14:10]), .b({5{1'b1}}), .eq(comparator_1_eq));  // open: gt, lt
  Comparator #(.width(5), .mode("unsigned")) comparator_2 (
    .a(float[14:10]), .b({5{1'b0}}), .eq(comparator_2_eq));  // open: gt, lt
  // Probe on negator_1_out
  assign xor_1_out = float[14:10] ^ 5'b01111;  // XOR_Gate xor_1, 5 bits wide
  Negator #(.width(5)) negator_1 (.in(xor_1_out), .out(negator_1_out));
  Shifter #(.width(32)) shifter_1 (.in(bit_extender_2_out), .\dist (negator_1_out), .out(shifter_1_out));
  Shifter #(.width(32), .shift("lr")) shifter_2 (.in(shifter_1_out), .\dist (5'b01010), .out(shifter_2_out));
  Comparator #(.width(5)) comparator_3 (.a(negator_1_out), .b({5{1'b0}}), .lt(comparator_3_lt));  // open: gt, eq
  Negator #(.width(32)) negator_2 (.in(shifter_2_out), .out(negator_2_out));
  or or_1 (or_1_out, comparator_1_eq, comparator_2_eq, comparator_3_lt);
  Multiplexer #(.width(32)) multiplexer_1 (
    .in0(shifter_2_out), .in1(negator_2_out), .out(multiplexer_1_out), .sel(float[15]));  // open: en
  Multiplexer #(.width(32)) multiplexer_2 (
    .in0(multiplexer_1_out), .in1({32{1'b0}}), .out(\int ), .sel(or_1_out));  // open: en
endmodule
