// Logisim project grf.circ as structural Verilog: 2 circuits, main circuit address
module grf (
  input  clk,
  input  reset,
  input  WE,
  input  [4:0] A1,
  input  [31:0] WD,
  input  [4:0] A3,
  input  [4:0] A2,
  output [31:0] RD1,
  output [31:0] RD2
);

  address address_1 (.\input (WD), .rst(reset), .clk(clk), .en(WE), .w(A3), .a(A1), .out(RD1));
  address address_2 (.\input (WD), .rst(reset), .clk(clk), .en(WE), .w(A3), .a(A2), .out(RD2));

  // Other names for the same wires on the sheet: rst = reset
endmodule

module address (
  input  [31:0] \input ,
  input  rst,
  input  clk,
  input  en,
  input  [4:0] w,
  input  [4:0] a,
  output [31:0] out
);

  wire [31:0] demultiplexer_1_out0, demultiplexer_1_out1, demultiplexer_1_out2, demultiplexer_1_out3,
       demultiplexer_1_out4, demultiplexer_1_out5, demultiplexer_1_out6, demultiplexer_1_out7,
       demultiplexer_1_out8, demultiplexer_1_out9, demultiplexer_1_out10, demultiplexer_1_out11,
       demultiplexer_1_out12, demultiplexer_1_out13, demultiplexer_1_out14, demultiplexer_1_out15,
       demultiplexer_1_out16, demultiplexer_1_out17, demultiplexer_1_out18, demultiplexer_1_out19,
       demultiplexer_1_out20, demultiplexer_1_out21, demultiplexer_1_out22, demultiplexer_1_out23,
       demultiplexer_1_out24, demultiplexer_1_out25, demultiplexer_1_out26, demultiplexer_1_out27,
       demultiplexer_1_out28, demultiplexer_1_out29, demultiplexer_1_out30, demultiplexer_1_out31,
       register_1_q, register_2_q, register_3_q, register_4_q, register_5_q, register_6_q, register_7_q,
       register_8_q, register_9_q, register_10_q, register_11_q, register_12_q, register_13_q, register_14_q,
       register_15_q, register_16_q, register_17_q, register_18_q, register_19_q, register_20_q,
       register_21_q, register_22_q, register_23_q, register_24_q, register_25_q, register_26_q,
       register_27_q, register_28_q, register_29_q, register_30_q, register_31_q, register_32_q;

  Demultiplexer #(.select(5), .width(32), .tristate("true")) demultiplexer_1 (
    .out0(demultiplexer_1_out0), .out1(demultiplexer_1_out1), .out2(demultiplexer_1_out2),
    .out3(demultiplexer_1_out3), .out4(demultiplexer_1_out4), .out5(demultiplexer_1_out5),
    .out6(demultiplexer_1_out6), .out7(demultiplexer_1_out7), .out8(demultiplexer_1_out8),
    .out9(demultiplexer_1_out9), .out10(demultiplexer_1_out10), .out11(demultiplexer_1_out11),
    .out12(demultiplexer_1_out12), .out13(demultiplexer_1_out13), .out14(demultiplexer_1_out14),
    .out15(demultiplexer_1_out15), .out16(demultiplexer_1_out16), .out17(demultiplexer_1_out17),
    .out18(demultiplexer_1_out18), .out19(demultiplexer_1_out19), .out20(demultiplexer_1_out20),
    .out21(demultiplexer_1_out21), .out22(demultiplexer_1_out22), .out23(demultiplexer_1_out23),
    .out24(demultiplexer_1_out24), .out25(demultiplexer_1_out25), .out26(demultiplexer_1_out26),
    .out27(demultiplexer_1_out27), .out28(demultiplexer_1_out28), .out29(demultiplexer_1_out29),
    .out30(demultiplexer_1_out30), .out31(demultiplexer_1_out31), .in(\input ), .sel(w));  // open: en
  Register #(.width(32)) register_1 (.D(demultiplexer_1_out0), .Q(register_1_q), .clk(clk), .clr(1'b1));  // open: en
  Register #(.width(32)) register_2 (.D(demultiplexer_1_out4), .en(en), .Q(register_2_q), .clk(clk), .clr(rst));
  Register #(.width(32)) register_3 (.D(demultiplexer_1_out8), .en(en), .Q(register_3_q), .clk(clk), .clr(rst));
  Register #(.width(32)) register_4 (.D(demultiplexer_1_out12), .en(en), .Q(register_4_q), .clk(clk), .clr(rst));
  Register #(.width(32)) register_5 (.D(demultiplexer_1_out16), .en(en), .Q(register_5_q), .clk(clk), .clr(rst));
  Register #(.width(32)) register_6 (.D(demultiplexer_1_out20), .en(en), .Q(register_6_q), .clk(clk), .clr(rst));
  Register #(.width(32)) register_7 (.D(demultiplexer_1_out24), .en(en), .Q(register_7_q), .clk(clk), .clr(rst));
  Register #(.width(32)) register_8 (.D(demultiplexer_1_out28), .en(en), .Q(register_8_q), .clk(clk), .clr(rst));
  Register #(.width(32)) register_9 (.D(demultiplexer_1_out1), .en(en), .Q(register_9_q), .clk(clk), .clr(rst));
  Register #(.width(32)) register_10 (.D(demultiplexer_1_out5), .en(en), .Q(register_10_q), .clk(clk), .clr(rst));
  Register #(.width(32)) register_11 (.D(demultiplexer_1_out9), .en(en), .Q(register_11_q), .clk(clk), .clr(rst));
  Register #(.width(32)) register_12 (.D(demultiplexer_1_out13), .en(en), .Q(register_12_q), .clk(clk), .clr(rst));
  Register #(.width(32)) register_13 (.D(demultiplexer_1_out17), .en(en), .Q(register_13_q), .clk(clk), .clr(rst));
  Register #(.width(32)) register_14 (.D(demultiplexer_1_out21), .en(en), .Q(register_14_q), .clk(clk), .clr(rst));
  Register #(.width(32)) register_15 (.D(demultiplexer_1_out25), .en(en), .Q(register_15_q), .clk(clk), .clr(rst));
  Register #(.width(32)) register_16 (.D(demultiplexer_1_out29), .en(en), .Q(register_16_q), .clk(clk), .clr(rst));
  Register #(.width(32)) register_17 (.D(demultiplexer_1_out2), .en(en), .Q(register_17_q), .clk(clk), .clr(rst));
  Register #(.width(32)) register_18 (.D(demultiplexer_1_out6), .en(en), .Q(register_18_q), .clk(clk), .clr(rst));
  Register #(.width(32)) register_19 (.D(demultiplexer_1_out10), .en(en), .Q(register_19_q), .clk(clk), .clr(rst));
  Register #(.width(32)) register_20 (.D(demultiplexer_1_out14), .en(en), .Q(register_20_q), .clk(clk), .clr(rst));
  Register #(.width(32)) register_21 (.D(demultiplexer_1_out18), .en(en), .Q(register_21_q), .clk(clk), .clr(rst));
  Register #(.width(32)) register_22 (.D(demultiplexer_1_out22), .en(en), .Q(register_22_q), .clk(clk), .clr(rst));
  Register #(.width(32)) register_23 (.D(demultiplexer_1_out26), .en(en), .Q(register_23_q), .clk(clk), .clr(rst));
  Register #(.width(32)) register_24 (.D(demultiplexer_1_out30), .en(en), .Q(register_24_q), .clk(clk), .clr(rst));
  Register #(.width(32)) register_25 (.D(demultiplexer_1_out3), .en(en), .Q(register_25_q), .clk(clk), .clr(rst));
  Register #(.width(32)) register_26 (.D(demultiplexer_1_out7), .en(en), .Q(register_26_q), .clk(clk), .clr(rst));
  Register #(.width(32)) register_27 (.D(demultiplexer_1_out11), .en(en), .Q(register_27_q), .clk(clk), .clr(rst));
  Register #(.width(32)) register_28 (.D(demultiplexer_1_out15), .en(en), .Q(register_28_q), .clk(clk), .clr(rst));
  Register #(.width(32)) register_29 (.D(demultiplexer_1_out19), .en(en), .Q(register_29_q), .clk(clk), .clr(rst));
  Register #(.width(32)) register_30 (.D(demultiplexer_1_out23), .en(en), .Q(register_30_q), .clk(clk), .clr(rst));
  Register #(.width(32)) register_31 (.D(demultiplexer_1_out27), .en(en), .Q(register_31_q), .clk(clk), .clr(rst));
  Register #(.width(32)) register_32 (.D(demultiplexer_1_out31), .en(en), .Q(register_32_q), .clk(clk), .clr(rst));
  Multiplexer #(.select(5), .width(32)) multiplexer_1 (
    .in0(register_1_q), .in1(register_9_q), .in2(register_17_q), .in3(register_25_q), .in4(register_2_q),
    .in5(register_10_q), .in6(register_18_q), .in7(register_26_q), .in8(register_3_q), .in9(register_11_q),
    .in10(register_19_q), .in11(register_27_q), .in12(register_4_q), .in13(register_12_q),
    .in14(register_20_q), .in15(register_28_q), .in16(register_5_q), .in17(register_13_q),
    .in18(register_21_q), .in19(register_29_q), .in20(register_6_q), .in21(register_14_q),
    .in22(register_22_q), .in23(register_30_q), .in24(register_7_q), .in25(register_15_q),
    .in26(register_23_q), .in27(register_31_q), .in28(register_8_q), .in29(register_16_q),
    .in30(register_24_q), .in31(register_32_q), .out(out), .sel(a));  // open: en
endmodule
