// Logisim project navigation.circ as structural Verilog: 3 circuits, main circuit navigation
module navigation (
  input  clk,
  input  reset,
  input  [1:0] dir,
  output arrive,
  output hit
);

  wire comparator_1_eq, not_1_out, register_2_q;
  wire [2:0] register_1_q, tran1_1_n0;

  Clock u_clk ();  // open: out
  tran1 tran1_1 (
    .in1(dir[1]), .in0(dir[0]), .s2(register_1_q[2]), .s1(register_1_q[1]), .s0(register_1_q[0]),
    .n2(tran1_1_n0[2]), .n1(tran1_1_n0[1]), .n0(tran1_1_n0[0]));
  Register #(.width(3)) register_1 (.D(tran1_1_n0), .Q(register_1_q), .clk(clk), .clr(reset));  // open: en
  Comparator #(.width(3), .mode("unsigned")) comparator_1 (
    .a(tran1_1_n0), .b(register_1_q), .eq(comparator_1_eq));  // open: gt, lt
  Register #(.width(1)) register_2 (.D(comparator_1_eq), .Q(register_2_q), .clk(clk), .clr(reset));  // open: en
  out1 out1_1 (.s2(register_1_q[2]), .s1(register_1_q[1]), .s0(register_1_q[0]), .ar(arrive));
  not not_1 (not_1_out, arrive);
  and and_1 (hit, not_1_out, register_2_q);

  // Other names for the same wires on the sheet: rst = reset
endmodule

module tran1 (
  input  in1,
  input  in0,
  input  s2,
  input  s1,
  input  s0,
  output n2,
  output n1,
  output n0
);

  wire and_1_out, and_2_out, and_3_out, and_4_out, and_5_out, and_6_out, and_7_out, and_8_out, and_9_out,
       and_10_out, and_11_out, not_1_out, not_2_out, not_3_out, not_4_out, not_5_out, not_6_out, not_7_out,
       not_8_out, not_9_out, not_10_out, not_11_out, not_12_out, not_13_out, not_14_out, not_15_out,
       not_16_out, not_17_out;

  not not_1 (not_1_out, in1);
  not not_2 (not_2_out, in0);
  not not_3 (not_3_out, s0);
  not not_4 (not_4_out, in1);
  not not_5 (not_5_out, in1);
  not not_6 (not_6_out, in0);
  not not_7 (not_7_out, in1);
  not not_8 (not_8_out, s1);
  not not_9 (not_9_out, in1);
  not not_10 (not_10_out, s0);
  not not_11 (not_11_out, in0);
  not not_12 (not_12_out, s0);
  not not_13 (not_13_out, in1);
  not not_14 (not_14_out, in0);
  not not_15 (not_15_out, s2);
  not not_16 (not_16_out, s1);
  not not_17 (not_17_out, in0);
  and and_1 (and_1_out, not_1_out, not_2_out, s1, not_3_out);
  and and_2 (and_2_out, not_4_out, in0, s1, s0);
  and and_3 (and_3_out, not_5_out, not_6_out, s0);
  and and_4 (and_4_out, not_7_out, not_8_out, s0);
  and and_5 (and_5_out, not_9_out, in0, s1, not_10_out);
  and and_6 (and_6_out, in1, not_11_out, s1, not_12_out);
  and and_7 (and_7_out, in1, in0, s1, s0);
  and and_8 (and_8_out, not_13_out, not_14_out, not_15_out, not_16_out);
  and and_9 (and_9_out, not_17_out, s1, s0);
  and and_10 (and_10_out, in1, in0, s0);
  and and_11 (and_11_out, in1, in0, s1);
  or or_1 (n2, and_1_out, and_2_out);
  or or_2 (n1, and_3_out, and_4_out, and_5_out, and_6_out, and_7_out);
  or or_3 (n0, and_8_out, and_9_out, and_10_out, and_11_out);
endmodule

module out1 (
  input  s2,
  input  s1,
  input  s0,
  output ar
);


  assign ar = s2;
endmodule
